// Logisim project AddressDedoder_8Bits.circ as structural Verilog: 1 circuit, main circuit addressDecoder_8bits
module addressDecoder_8bits (
  input  A3,
  input  A2,
  input  A1,
  input  A0,
  input  Enable,
  output DF,
  output DE,
  output DD,
  output DC,
  output DB,
  output DA,
  output D9,
  output D8,
  output D7,
  output D6,
  output D5,
  output D4,
  output D3,
  output D2,
  output D1,
  output D0
);

  wire and_1_out, and_2_out, and_3_out, and_4_out, and_5_out, and_6_out, and_7_out, and_8_out, and_9_out,
       and_10_out, and_11_out, and_12_out, and_13_out, and_14_out, and_15_out, and_16_out, not_1_out,
       not_2_out, not_3_out, not_4_out;

  not not_1 (not_1_out, A3);
  not not_2 (not_2_out, A2);
  not not_3 (not_3_out, A1);
  not not_4 (not_4_out, A0);
  and and_1 (and_1_out, A3, A2, A1, A0);
  assign DF = Enable ? and_1_out : 1'bz;  // Controlled_Buffer controlled_buffer_1
  and and_2 (and_2_out, A3, A2, A1, not_4_out);
  assign DE = Enable ? and_2_out : 1'bz;  // Controlled_Buffer controlled_buffer_2
  and and_3 (and_3_out, A3, A2, A0, not_3_out);
  assign DD = Enable ? and_3_out : 1'bz;  // Controlled_Buffer controlled_buffer_3
  and and_4 (and_4_out, A3, A2, not_3_out, not_4_out);
  assign DC = Enable ? and_4_out : 1'bz;  // Controlled_Buffer controlled_buffer_4
  and and_5 (and_5_out, A3, not_2_out, A1, A0);
  assign DB = Enable ? and_5_out : 1'bz;  // Controlled_Buffer controlled_buffer_5
  and and_6 (and_6_out, A3, not_2_out, A1, not_4_out);
  assign DA = Enable ? and_6_out : 1'bz;  // Controlled_Buffer controlled_buffer_6
  and and_7 (and_7_out, A3, not_2_out, not_3_out, A0);
  assign D9 = Enable ? and_7_out : 1'bz;  // Controlled_Buffer controlled_buffer_7
  and and_8 (and_8_out, A3, not_2_out, not_3_out, not_4_out);
  assign D8 = Enable ? and_8_out : 1'bz;  // Controlled_Buffer controlled_buffer_8
  and and_9 (and_9_out, not_1_out, A2, A1, A0);
  assign D7 = Enable ? and_9_out : 1'bz;  // Controlled_Buffer controlled_buffer_9
  and and_10 (and_10_out, not_4_out, A1, A2, not_1_out);
  assign D6 = Enable ? and_10_out : 1'bz;  // Controlled_Buffer controlled_buffer_10
  and and_11 (and_11_out, not_3_out, not_1_out, A2, A0);
  assign D5 = Enable ? and_11_out : 1'bz;  // Controlled_Buffer controlled_buffer_11
  and and_12 (and_12_out, not_4_out, not_3_out, A2, not_1_out);
  assign D4 = Enable ? and_12_out : 1'bz;  // Controlled_Buffer controlled_buffer_12
  and and_13 (and_13_out, not_1_out, not_2_out, A0, A1);
  assign D3 = Enable ? and_13_out : 1'bz;  // Controlled_Buffer controlled_buffer_13
  and and_14 (and_14_out, not_4_out, not_3_out, A1, not_1_out);
  assign D2 = Enable ? and_14_out : 1'bz;  // Controlled_Buffer controlled_buffer_14
  and and_15 (and_15_out, not_1_out, not_2_out, not_3_out, A0);
  assign D1 = Enable ? and_15_out : 1'bz;  // Controlled_Buffer controlled_buffer_15
  and and_16 (and_16_out, not_4_out, not_3_out, not_2_out, not_1_out);
  assign D0 = Enable ? and_16_out : 1'bz;  // Controlled_Buffer controlled_buffer_16
endmodule
