// Logisim project Cpu_simulation.circ as structural Verilog: 2 circuits, main circuit main
module main (
  input  run,
  input  hlt,
  input  in_3,
  input  MAR_Clear,
  input  [7:0] in_5,
  input  reset,
  input  in_7,
  input  in_8,
  input  in_9,
  input  [3:0] in_10,
  input  deco_ena,
  input  in_12,
  input  [2:0] in_13,
  input  in_14,
  input  out_load,
  input  CLR,
  input  in_17,
  input  in_18,
  input  in_19,
  input  [7:0] in_20,
  input  ir_clear,
  input  opc_dec_ena,
  output [3:0] out_23,
  output [7:0] out_24,
  output RAM_OE,
  output carry,
  output [3:0] out_27,
  output out_28,
  output [3:0] out_29,
  output [7:0] out_30,
  output [7:0] out_out,
  output [2:0] out_32,
  output [7:0] out_33,
  output [7:0] out_34,
  output IR_to_MAR,
  output mem_op,
  output B_Load
);

  wire and_1_out, and_2_out, and_5_out, decoder_1_out0, decoder_1_out1, decoder_1_out2, decoder_1_out3,
       decoder_1_out4, decoder_1_out5, decoder_2_out0, decoder_2_out1, decoder_2_out2, decoder_2_out3,
       decoder_2_out4, decoder_2_out5, decoder_2_out6, decoder_2_out7, not_1_out, or_1_out, step_out;
  wire [3:0] counter_2_q;
  wire [7:0] adder_1_out, register_1_q;

  and and_1 (and_1_out, step_out, run);
  not not_1 (not_1_out, hlt);
  Counter #(.max('h5), .width(3)) counter_1 (
    .clr(in_7), .load(in_8), .up(in_9), .count(deco_ena), .clk(and_2_out), .D(in_13), .carry(out_28),
    .Q(out_32));
  and and_2 (and_2_out, and_1_out, not_1_out);
  LedBar ledbar_1 (
    .led0(decoder_1_out0), .led1(decoder_1_out1), .led2(decoder_1_out2), .led3(decoder_1_out3),
    .led4(decoder_1_out4), .led5(decoder_1_out5));  // open: led6, led7
  Decoder #(.select(3)) decoder_1 (
    .out0(decoder_1_out0), .out1(decoder_1_out1), .out2(decoder_1_out2), .out3(decoder_1_out3),
    .out4(decoder_1_out4), .out5(decoder_1_out5), .sel(out_32), .en(in_12));  // open: out6, out7
  or or_1 (or_1_out, decoder_1_out0, IR_to_MAR);
  Register register_1 (.D(in_20), .en(decoder_1_out1), .clk(and_2_out), .Q(register_1_q), .clr(ir_clear));
  Register #(.width(4)) register_2 (.D(out_29), .en(or_1_out), .clk(and_2_out), .Q(out_23), .clr(MAR_Clear));
  Counter #(.max('hf), .width(4)) counter_2 (
    .clr(reset), .load(decoder_1_out1), .up(decoder_1_out1), .count(decoder_1_out1), .clk(and_2_out),
    .D(in_10), .carry(carry), .Q(counter_2_q));
  Hex_Digit_Display hex_digit_display_1 (.value(register_1_q[3:0]));  // open: dp
  Hex_Digit_Display hex_digit_display_2 (.value(register_1_q[7:4]));  // open: dp
  assign out_27 = counter_2_q;  // Buffer buffer_1, 4 bits wide
  Decoder #(.select(4)) decoder_2 (
    .out0(decoder_2_out0), .out1(decoder_2_out1), .out2(decoder_2_out2), .out3(decoder_2_out3),
    .out4(decoder_2_out4), .out5(decoder_2_out5), .out6(decoder_2_out6), .out7(decoder_2_out7),
    .sel(register_1_q[7:4]), .en(opc_dec_ena));  // open: out8, out9, out10, out11, out12, out13, out14, out15
  Multiplexer #(.width(4)) multiplexer_1 (.in0(out_27), .in1(register_1_q[3:0]), .out(out_29), .sel(IR_to_MAR));
  LedBar ledbar_2 (
    .led0(decoder_2_out0), .led1(decoder_2_out1), .led2(decoder_2_out2), .led3(decoder_2_out3),
    .led4(decoder_2_out4), .led5(decoder_2_out5), .led6(decoder_2_out6), .led7(decoder_2_out7));
  or or_2 (RAM_OE, decoder_1_out1, B_Load);
  or or_3 (mem_op, decoder_2_out0, decoder_2_out1, decoder_2_out2);
  RAM #(.addrWidth(4)) ram_1 (.addr(out_23), .we(in_3), .oe(RAM_OE), .clk(and_2_out), .din(in_5), .dout(out_24));
  and and_3 (IR_to_MAR, decoder_1_out3, mem_op);
  Button step (.out(step_out));
  and and_4 (B_Load, decoder_2_out2, decoder_1_out4);
  Register register_3 (.D(out_24), .en(in_14), .clk(and_2_out), .Q(out_30), .clr(in_17));
  Register register_4 (.D(out_24), .en(in_18), .clk(and_2_out), .Q(out_34), .clr(in_19));
  Adder adder_1 (.a(out_30), .b(out_34), .out(adder_1_out));  // open: cin, cout
  assign out_33 = and_5_out ? adder_1_out : 8'bz;  // Controlled_Buffer controlled_buffer_1
  and and_5 (and_5_out, decoder_2_out2, decoder_1_out5);
  Register register_5 (.D(out_33), .en(out_load), .clk(and_2_out), .Q(out_out), .clr(CLR));

  // Notes on the sheet:
  //   6 State Design (Structured Controlled Unit)
  //   T State Decoder
  //   Memory Address Register
  //   Program Counter
  //   Instruction Register
  //   operand
  //   opcode
  //   It is ADD also
  //   Register A
  //   Register B
  //   carry flag is there here, lets see later
  //   Arithmetic Logic Unit
endmodule

module \clocking  (
  input  run,
  input  hlt,
  output clk
);

  wire and_1_out, not_1_out, step_out;

  Button step (.out(step_out));
  not not_1 (not_1_out, hlt);
  and and_1 (and_1_out, step_out, run);
  and and_2 (clk, and_1_out, not_1_out);
endmodule
