// Logisim project Decoder_8_bits_to_7_segment.circ as structural Verilog: 1 circuit, main circuit Decoder_8to7_Segment
module Decoder_8to7_Segment (
  input  I0,
  input  I1,
  input  I2,
  input  I3,
  input  I4,
  input  I5,
  input  I6,
  input  I7,
  output g3,
  output f3,
  output e3,
  output d3,
  output c3,
  output b3,
  output a3,
  output g2,
  output f2,
  output e2,
  output d2,
  output c2,
  output b2,
  output a2,
  output g1,
  output f1,
  output e1,
  output d1,
  output c1,
  output b1,
  output a1
);

  ROM #(.dataWidth(21)) rom_1 (
    .addr({I7, I6, I5, I4, I3, I2, I1, I0}),
    .data({g3, f3, e3, d3, c3, b3, a3, g2, f2, e2, d2, c2, b2, a2, g1, f1, e1, d1, c1, b1, a1}));

  // Notes on the sheet:
  //   contents of rom_1 (hex, n*v repeats v):
  //   337f 336f 36bf 3686 36db 36cf 36e6 36ed 36fd 3687 36ff 36ef 3ebf 3e86 3edb 3ecf 3ee6 3eed 3efd 3e87
  //   3eff 3eef 3bf 386 3db 3cf 3e6 3ed 3fd 387 3ff 3ef 3fbf 3f86 3fdb 3fcf 3fe6 3fed 3ffd 3f87 3fff 3fef
  //   37bf 3786 37db 37cf 37e6 37ed 37fd 3787 37ff 37eff 19fbf 19f86 19fdb 19fcf 19fe6 19fed 19ffd 19f87
  //   19fff 19fef 1833f 18306 1835b 1834f 18366 1836d 1837d 18307 1837f 1836f 1adbf 1ad86 1addb 1adcf
  //   1ade6 1aded 1adfd 1ad87 1adff 1adef 1a7bf 1a786 1a7db 1a7cf 1a7e6 1a7ed 1a7fd 1a787 1a7ff 1a7ef
  //   1b33f 1b306 1b35b 1b34f 1b366 1b36d 1b37d 1b307 1b37f 1b36f 1b6bf 1b686 1b6db 1b6cf 1b6ef 1b6ed
  //   1b6fd 1b687 1b6ff 1b6ef 1bebf 1be86 1bedb 1becf 1bee6 1beed 1befd 1be87 1beff 1beef 183bf 18386
  //   183db 183cf 183e6 183ed 183fd 18387 183ff 183ef 1bfbf 1bf86 1bfdb 1bfcf 1bfe6 1bfed 1bffd bf87 1bfff
  //   1bfef 1b7bf 1b786 1b7db 1b7cf 1b7e6 1b7ed 1b7fd 1b787 1b7ff 1b7ef 16dfbf 16df86 16dfdb 16dfcf 16dfe6
  //   16dfed 16dffd 16df87 16dfff 16dfef 16c33f 16c306 16c35b 16c34f 16c366 16c36d 16c37d 16c307 16c37f
  //   16c36f 16edbf 16ed86 16eddb 16edcf 16ede6 16eded 16edfd 16ed87 16edff 16edef 16e7bf 16e786 16e7db
  //   16e7cf 16e7e6 16e7ed 16e7fd 16e787 16e7ff 16e7ef 16f33f 16f306 16f35b 16f34f 16f366 16f36d 16f37d
  //   16f307 16f37f 16f36f 16f6bf 16f686 16f6db 16f6cf 16f6e6 16f6ed
endmodule
