// Logisim project Full_adder.circ as structural Verilog: 1 circuit, main circuit Full_adder
module Full_adder (
  input  A,
  input  B,
  input  Ci,
  output E,
  output Co
);

  wire and_1_out, and_2_out, xor_1_out;

  xor xor_1 (xor_1_out, A, B);
  and and_1 (and_1_out, xor_1_out, Ci);
  and and_2 (and_2_out, A, B);
  xor xor_2 (E, xor_1_out, Ci);
  or or_1 (Co, and_1_out, and_2_out);
endmodule
