// Logisim project Grounder_4Bits.circ as structural Verilog: 1 circuit, main circuit Grounder_4bits
module Grounder_4bits (
  input  IP,
  output G3,
  output G2,
  output G1,
  output G0
);

  assign G3 = IP ? 1'b0 : 1'bz;  // Controlled_Buffer controlled_buffer_1
  assign G2 = IP ? 1'b0 : 1'bz;  // Controlled_Buffer controlled_buffer_2
  assign G1 = IP ? 1'b0 : 1'bz;  // Controlled_Buffer controlled_buffer_3
  assign G0 = IP ? 1'b0 : 1'bz;  // Controlled_Buffer controlled_buffer_4
endmodule
