// Logisim project Instruction_decoder.circ as structural Verilog: 3 circuits, main circuit Instruction_decoder
module Instruction_decoder (
  input  ZF,
  input  CF,
  input  OP0,
  input  OP1,
  input  OP2,
  input  OP3,
  input  OP4,
  input  Clear,
  input  CLK,
  input  in_10,
  input  in_11,
  output FI,
  output HL,
  output AI,
  output AO,
  output EO,
  output SU,
  output BI,
  output BO,
  output MI,
  output RW,
  output RR,
  output II,
  output IR,
  output CE,
  output CO,
  output JP,
  output OI,
  output S7,
  output S6,
  output S5,
  output S4,
  output S3,
  output S2,
  output S1,
  output S0
);

  wire counter_8bits_1_o3, decoder_8bits_1_d8, not_1_out, not_2_out, or_1_out;
  wire [2:0] counter_8bits_1_o0;

  not not_1 (not_1_out, in_10);
  or or_1 (or_1_out, Clear, IR, decoder_8bits_1_d8);
  not not_2 (not_2_out, CLK);
  Counter_8bits counter_8bits_1 (
    .Clock(not_2_out), .COut(in_10), .CEnable(in_10), .CWrite(not_1_out), .CReset(or_1_out),
    .O3(counter_8bits_1_o3), .O2(counter_8bits_1_o0[2]), .O1(counter_8bits_1_o0[1]),
    .O0(counter_8bits_1_o0[0]));  // open: I7, I6, I5, I4, I3, I2, I1, I0, D7, D6, D5, D4, D3, D2, D1, D0, O7, O6, O5, O4
  Decoder_8bits decoder_8bits_1 (
    .A3(counter_8bits_1_o3), .A2(counter_8bits_1_o0[2]), .A1(counter_8bits_1_o0[1]),
    .A0(counter_8bits_1_o0[0]), .Enable(in_11), .D8(decoder_8bits_1_d8), .D7(S7), .D6(S6), .D5(S5), .D4(S4),
    .D3(S3), .D2(S2), .D1(S1), .D0(S0));  // open: DF, DE, DD, DC, DB, DA, D9
  ROM #(.addrWidth(10), .dataWidth(17)) rom_1 (
    .addr({OP4, OP3, OP2, OP1, OP0, CF, ZF, counter_8bits_1_o0}),
    .data({FI, HL, AI, AO, EO, SU, BI, BO, MI, RW, RR, II, IR, CE, CO, JP, OI}));

  // Notes on the sheet:
  //   contents of rom_1 (hex, n*v repeats v):
  //   104 68 10 5*0 104 68 10 5*0 104 68 10 5*0 104 68 10 5*0 104 68 8000 10 4*0 104 68 8000 10 4*0 104 68
  //   8000 10 4*0 104 68 8000 10 4*0 104 68 10c 4040 10 0 0 0 104 68 10c 4040 10 0 0 0 104 68 10c 4040 10
  //   0 0 0 104 68 10c 4040 10 0 0 0 104 68 10c 140 4040 10 0 0 104 68 10c 140 4040 10 0 0 104 68 10c 140
  //   4040 10 0 0 104 68 10c 140 4040 10 0 0 104 68 10c 140 2080 10 0 0 104 68 10c 140 2080 10 0 0 104 68
  //   10c 140 2080 10 0 0 104 68 10c 140 2080 10 0 0 104 68 10c 440 10 0 0 0 104 68 10c 440 10 0 0 0 104
  //   68 10c 440 10 0 0 0 104 68 10c 440 10 0 0 0 104 68 10c 140 440 10 0 0 104 68 10c 140 440 10 0 0 104
  //   68 10c 140 440 10 0 0 104 68 10c 140 440 10 0 0 104 68 10c 140 280 10 0 0 104 68 10c 140 280 10 0 0
  //   104 68 c 140 280 10 0 0 104 68 10c 140 280 10 0 0 104 68 10c 440 15000 10 0 0 104 68 10c 440 15000
  //   10 0 0 104 68 10c 440 15000 10 0 0 104 68 10c 440 15000 10 0 0 104 68 10c 140 440 15000 10 0 104 68
  //   10c 140 440 15000 10 0 104 68 10c 140 440 15000 10 0 104 68 10c 140 440 15000 10 0 104 68 10c c40
  //   15800 10 0 0 104 68 10c c40 15800 10 0 0 104 68 10c c40 15800 10 0 0 104 68 10c c40 15800 10 0 0 104
  //   68 10c 140 c40 15800 10 0 104 68 10c 140 c40 15800 10 0 104 668 10c 140 c40 15800 10 0 104 68 10c
  //   140 c40 15800 10 0 104 68 2001 10 4*0 104 68 2001 10 4*0 104 68 2001 10 4*0 104 68 2001 10 4*0 104
  //   68 201 10 4*0 104 68 201 10 4*0 104 68 201 10 4*0 104 68 10c 10 4*0 10 68 10c 41 10 0 0 0 104 68 10c
  //   41 10 0 0 0 104 68 10c 41 10 0 0 0 104 68 10c 41 10 0 0 0 104 68 10c 140 41 10 0 0 104 68 10c 140 41
  //   10 0 0 104 68 10c 140 41 10 0 0 104 68 10c 140 41 0 0 0 104 68 10c 42 10 0 0 0 104 68 10c 42 10 0 0
  //   0 104 68 10c 42 10 0 0 0 104 68 10c 42 10 0 0 0 104 68 8 10 4*0 104 68 10c 42 10 0 0 0 104 68 8 10
  //   4*0 104 68 10c 42 10 0 0 0 104 68 8 10 4*0 104 68 8 1 4*0 104 68 10c 42 10 0 0 0 104 68 10c 42 10
endmodule

module Counter_8bits (
  input  I7,
  input  I6,
  input  I5,
  input  I4,
  input  I3,
  input  I2,
  input  I1,
  input  I0,
  input  Clock,
  input  COut,
  input  CEnable,
  input  CWrite,
  input  CReset,
  output D7,
  output D6,
  output D5,
  output D4,
  output D3,
  output D2,
  output D1,
  output D0,
  output O7,
  output O6,
  output O5,
  output O4,
  output O3,
  output O2,
  output O1,
  output O0
);

  wire and_1_out, and_2_out, and_3_out, and_4_out, and_5_out, and_6_out, and_7_out, and_8_out, and_9_out,
       and_10_out, and_11_out, and_12_out, and_13_out, and_14_out, and_15_out, and_16_out, j_k_ff_2_qn,
       j_k_ff_3_qn, j_k_ff_4_qn, j_k_ff_5_qn, j_k_ff_6_qn, j_k_ff_7_qn, j_k_ff_8_qn, not_1_out, not_2_out,
       not_3_out, not_4_out, not_5_out, not_6_out, not_7_out, not_8_out, or_1_out, or_2_out, or_3_out,
       or_4_out, or_5_out, or_6_out, or_7_out, or_8_out;

  and and_1 (and_1_out, CWrite, I7, Clock);
  or or_1 (or_1_out, CReset, and_2_out);
  J_K_Flip_Flop j_k_ff_1 (
    .J(CEnable), .K(CEnable), .clk(j_k_ff_2_qn), .Q(D7), .preset(and_1_out), .reset(or_1_out));  // open: Qn
  not not_1 (not_1_out, I7);
  and and_2 (and_2_out, CWrite, not_1_out, Clock);
  not not_2 (not_2_out, I6);
  and and_3 (and_3_out, CWrite, I6, Clock);
  and and_4 (and_4_out, CWrite, not_2_out, Clock);
  or or_2 (or_2_out, CReset, and_4_out);
  J_K_Flip_Flop j_k_ff_2 (
    .J(CEnable), .K(CEnable), .clk(j_k_ff_3_qn), .Q(D6), .Qn(j_k_ff_2_qn), .preset(and_3_out),
    .reset(or_2_out));
  and and_5 (and_5_out, CWrite, I5, Clock);
  or or_3 (or_3_out, CReset, and_6_out);
  J_K_Flip_Flop j_k_ff_3 (
    .J(CEnable), .K(CEnable), .clk(j_k_ff_4_qn), .Q(D5), .Qn(j_k_ff_3_qn), .preset(and_5_out),
    .reset(or_3_out));
  not not_3 (not_3_out, I5);
  and and_6 (and_6_out, CWrite, not_3_out, Clock);
  not not_4 (not_4_out, I4);
  and and_7 (and_7_out, CWrite, I4, Clock);
  and and_8 (and_8_out, CWrite, not_4_out, Clock);
  or or_4 (or_4_out, CReset, and_8_out);
  J_K_Flip_Flop j_k_ff_4 (
    .J(CEnable), .K(CEnable), .clk(j_k_ff_5_qn), .Q(D4), .Qn(j_k_ff_4_qn), .preset(and_7_out),
    .reset(or_4_out));
  and and_9 (and_9_out, CWrite, I3, Clock);
  or or_5 (or_5_out, CReset, and_11_out);
  J_K_Flip_Flop j_k_ff_5 (
    .J(CEnable), .K(CEnable), .clk(j_k_ff_6_qn), .Q(D3), .Qn(j_k_ff_5_qn), .preset(and_9_out),
    .reset(or_5_out));
  not not_5 (not_5_out, I3);
  and and_10 (and_10_out, CWrite, I2, Clock);
  and and_11 (and_11_out, CWrite, not_5_out, Clock);
  J_K_Flip_Flop j_k_ff_6 (
    .J(CEnable), .K(CEnable), .clk(j_k_ff_7_qn), .Q(D2), .Qn(j_k_ff_6_qn), .preset(and_10_out),
    .reset(or_6_out));
  not not_6 (not_6_out, I2);
  and and_12 (and_12_out, CWrite, not_6_out, Clock);
  or or_6 (or_6_out, CReset, and_12_out);
  and and_13 (and_13_out, CWrite, I1, Clock);
  or or_7 (or_7_out, CReset, and_14_out);
  J_K_Flip_Flop j_k_ff_7 (
    .J(CEnable), .K(CEnable), .clk(j_k_ff_8_qn), .Q(D1), .Qn(j_k_ff_7_qn), .preset(and_13_out),
    .reset(or_7_out));
  not not_7 (not_7_out, I1);
  and and_14 (and_14_out, CWrite, not_7_out, Clock);
  and and_15 (and_15_out, CWrite, I0, Clock);
  J_K_Flip_Flop j_k_ff_8 (
    .J(CEnable), .K(CEnable), .clk(Clock), .Q(D0), .Qn(j_k_ff_8_qn), .preset(and_15_out), .reset(or_8_out));
  not not_8 (not_8_out, I0);
  and and_16 (and_16_out, CWrite, not_8_out, Clock);
  or or_8 (or_8_out, CReset, and_16_out);
  assign O7 = COut ? D7 : 1'bz;  // Controlled_Buffer controlled_buffer_1
  assign O6 = COut ? D6 : 1'bz;  // Controlled_Buffer controlled_buffer_2
  assign O5 = COut ? D5 : 1'bz;  // Controlled_Buffer controlled_buffer_3
  assign O4 = COut ? D4 : 1'bz;  // Controlled_Buffer controlled_buffer_4
  assign O3 = COut ? D3 : 1'bz;  // Controlled_Buffer controlled_buffer_5
  assign O2 = COut ? D2 : 1'bz;  // Controlled_Buffer controlled_buffer_6
  assign O1 = COut ? D1 : 1'bz;  // Controlled_Buffer controlled_buffer_7
  assign O0 = COut ? D0 : 1'bz;  // Controlled_Buffer controlled_buffer_8
endmodule

module Decoder_8bits (
  input  A3,
  input  A2,
  input  A1,
  input  A0,
  input  Enable,
  output DF,
  output DE,
  output DD,
  output DC,
  output DB,
  output DA,
  output D9,
  output D8,
  output D7,
  output D6,
  output D5,
  output D4,
  output D3,
  output D2,
  output D1,
  output D0
);

  wire and_1_out, and_2_out, and_3_out, and_4_out, and_5_out, and_6_out, and_7_out, and_8_out, and_9_out,
       and_10_out, and_11_out, and_12_out, and_13_out, and_14_out, and_15_out, and_16_out, not_1_out,
       not_2_out, not_3_out, not_4_out;

  not not_1 (not_1_out, A3);
  not not_2 (not_2_out, A2);
  not not_3 (not_3_out, A1);
  not not_4 (not_4_out, A0);
  and and_1 (and_1_out, A3, A2, A1, A0);
  assign DF = Enable ? and_1_out : 1'bz;  // Controlled_Buffer controlled_buffer_1
  and and_2 (and_2_out, A3, A2, A1, not_4_out);
  assign DE = Enable ? and_2_out : 1'bz;  // Controlled_Buffer controlled_buffer_2
  and and_3 (and_3_out, A3, A2, A0, not_3_out);
  assign DD = Enable ? and_3_out : 1'bz;  // Controlled_Buffer controlled_buffer_3
  and and_4 (and_4_out, A3, A2, not_3_out, not_4_out);
  assign DC = Enable ? and_4_out : 1'bz;  // Controlled_Buffer controlled_buffer_4
  and and_5 (and_5_out, A3, not_2_out, A1, A0);
  assign DB = Enable ? and_5_out : 1'bz;  // Controlled_Buffer controlled_buffer_5
  and and_6 (and_6_out, A3, not_2_out, A1, not_4_out);
  assign DA = Enable ? and_6_out : 1'bz;  // Controlled_Buffer controlled_buffer_6
  and and_7 (and_7_out, A3, not_2_out, not_3_out, A0);
  assign D9 = Enable ? and_7_out : 1'bz;  // Controlled_Buffer controlled_buffer_7
  and and_8 (and_8_out, A3, not_2_out, not_3_out, not_4_out);
  assign D8 = Enable ? and_8_out : 1'bz;  // Controlled_Buffer controlled_buffer_8
  and and_9 (and_9_out, not_1_out, A2, A1, A0);
  assign D7 = Enable ? and_9_out : 1'bz;  // Controlled_Buffer controlled_buffer_9
  and and_10 (and_10_out, not_4_out, A1, A2, not_1_out);
  assign D6 = Enable ? and_10_out : 1'bz;  // Controlled_Buffer controlled_buffer_10
  and and_11 (and_11_out, not_3_out, not_1_out, A2, A0);
  assign D5 = Enable ? and_11_out : 1'bz;  // Controlled_Buffer controlled_buffer_11
  and and_12 (and_12_out, not_4_out, not_3_out, A2, not_1_out);
  assign D4 = Enable ? and_12_out : 1'bz;  // Controlled_Buffer controlled_buffer_12
  and and_13 (and_13_out, not_1_out, not_2_out, A0, A1);
  assign D3 = Enable ? and_13_out : 1'bz;  // Controlled_Buffer controlled_buffer_13
  and and_14 (and_14_out, not_4_out, not_3_out, A1, not_1_out);
  assign D2 = Enable ? and_14_out : 1'bz;  // Controlled_Buffer controlled_buffer_14
  and and_15 (and_15_out, not_1_out, not_2_out, not_3_out, A0);
  assign D1 = Enable ? and_15_out : 1'bz;  // Controlled_Buffer controlled_buffer_15
  and and_16 (and_16_out, not_4_out, not_3_out, not_2_out, not_1_out);
  assign D0 = Enable ? and_16_out : 1'bz;  // Controlled_Buffer controlled_buffer_16
endmodule
