// Logisim project Register_2_Bits.circ as structural Verilog: 1 circuit, main circuit register_2bits
module register_2bits (
  input  I1,
  input  I0,
  input  Clock,
  input  Load,
  input  Reset,
  input  Enable,
  output B1,
  output B0,
  output O1,
  output O0
);

  Register #(.width(1)) register_1 (.D(I1), .en(Load), .clk(Clock), .Q(B1), .clr(Reset));
  Register #(.width(1)) register_2 (.D(I0), .en(Load), .clk(Clock), .Q(B0), .clr(Reset));
  assign O1 = Enable ? B1 : 1'bz;  // Controlled_Buffer controlled_buffer_1
  assign O0 = Enable ? B0 : 1'bz;  // Controlled_Buffer controlled_buffer_2
endmodule
