// Logisim project Register_8Bit.circ as structural Verilog: 1 circuit, main circuit register_8bits
module register_8bits (
  input  I2,
  input  I1,
  input  I6,
  input  I5,
  input  I4,
  input  I3,
  input  I0,
  input  I7,
  input  Clock,
  input  Load,
  input  Reset,
  input  Enable,
  output B7,
  output D07,
  output B6,
  output D06,
  output B5,
  output D05,
  output B4,
  output D04,
  output B3,
  output D03,
  output B2,
  output D02,
  output B1,
  output D01,
  output B0,
  output D00
);

  Register #(.width(1)) register_1 (.D(I7), .en(Load), .clk(Clock), .Q(B7), .clr(Reset));
  Register #(.width(1)) register_2 (.D(I6), .en(Load), .clk(Clock), .Q(B6), .clr(Reset));
  Register #(.width(1)) register_3 (.D(I5), .en(Load), .clk(Clock), .Q(B5), .clr(Reset));
  Register #(.width(1)) register_4 (.D(I4), .en(Load), .clk(Clock), .Q(B4), .clr(Reset));
  Register #(.width(1)) register_5 (.D(I3), .en(Load), .clk(Clock), .Q(B3), .clr(Reset));
  Register #(.width(1)) register_6 (.D(I2), .en(Load), .clk(Clock), .Q(B2), .clr(Reset));
  Register #(.width(1)) register_7 (.D(I1), .en(Load), .clk(Clock), .Q(B1), .clr(Reset));
  Register #(.width(1)) register_8 (.D(I0), .en(Load), .clk(Reset), .Q(B0), .clr(Reset));
  assign D07 = Enable ? B7 : 1'bz;  // Controlled_Buffer controlled_buffer_1
  assign D06 = Enable ? B6 : 1'bz;  // Controlled_Buffer controlled_buffer_2
  assign D05 = Enable ? B5 : 1'bz;  // Controlled_Buffer controlled_buffer_3
  assign D04 = Enable ? B4 : 1'bz;  // Controlled_Buffer controlled_buffer_4
  assign D03 = Enable ? B3 : 1'bz;  // Controlled_Buffer controlled_buffer_5
  assign D02 = Enable ? B2 : 1'bz;  // Controlled_Buffer controlled_buffer_6
  assign D01 = Enable ? B1 : 1'bz;  // Controlled_Buffer controlled_buffer_7
  assign D00 = Enable ? B0 : 1'bz;  // Controlled_Buffer controlled_buffer_8
endmodule
