// Logisim project Reverser_8_Bits.circ as structural Verilog: 1 circuit, main circuit reverser_8bits
module reverser_8bits (
  input  IP_1,
  input  IP_2,
  input  IP_3,
  input  IP_4,
  input  IP_5,
  input  IP_6,
  input  IP_7,
  input  IP_8,
  output OP_1,
  output OP_2,
  output OP_3,
  output OP_4,
  output OP_5,
  output OP_6,
  output OP_7,
  output OP_8
);


  assign OP_1 = IP_8;
  assign OP_2 = IP_7;
  assign OP_3 = IP_6;
  assign OP_4 = IP_5;
  assign OP_5 = IP_4;
  assign OP_6 = IP_3;
  assign OP_7 = IP_2;
  assign OP_8 = IP_1;
endmodule
