// Logisim project pgloader_coun.circ as structural Verilog: 2 circuits, main circuit pcloader
module counterr (
  input  I7,
  input  I6,
  input  I5,
  input  I4,
  input  I3,
  input  I2,
  input  I1,
  input  I0,
  input  Clock,
  input  COut,
  input  CEnable,
  input  CWrite,
  input  CReset,
  output D7,
  output D6,
  output D5,
  output D4,
  output D3,
  output D2,
  output D1,
  output D0,
  output O7,
  output O6,
  output O5,
  output O4,
  output O3,
  output O2,
  output O1,
  output O0
);

  wire and_1_out, and_2_out, and_3_out, and_4_out, and_5_out, and_6_out, and_7_out, and_8_out, and_9_out,
       and_10_out, and_11_out, and_12_out, and_13_out, and_14_out, and_15_out, and_16_out, j_k_ff_2_qn,
       j_k_ff_3_qn, j_k_ff_4_qn, j_k_ff_5_qn, j_k_ff_6_qn, j_k_ff_7_qn, j_k_ff_8_qn, not_1_out, not_2_out,
       not_3_out, not_4_out, not_5_out, not_6_out, not_7_out, not_8_out, or_1_out, or_2_out, or_3_out,
       or_4_out, or_5_out, or_6_out, or_7_out, or_8_out;

  and and_1 (and_1_out, CWrite, I7, Clock);
  or or_1 (or_1_out, CReset, and_2_out);
  J_K_Flip_Flop j_k_ff_1 (
    .J(CEnable), .K(CEnable), .clk(j_k_ff_2_qn), .Q(D7), .preset(and_1_out), .reset(or_1_out));  // open: Qn
  not not_1 (not_1_out, I7);
  and and_2 (and_2_out, CWrite, not_1_out, Clock);
  not not_2 (not_2_out, I6);
  and and_3 (and_3_out, CWrite, I6, Clock);
  and and_4 (and_4_out, CWrite, not_2_out, Clock);
  or or_2 (or_2_out, CReset, and_4_out);
  J_K_Flip_Flop j_k_ff_2 (
    .J(CEnable), .K(CEnable), .clk(j_k_ff_3_qn), .Q(D6), .Qn(j_k_ff_2_qn), .preset(and_3_out),
    .reset(or_2_out));
  and and_5 (and_5_out, CWrite, I5, Clock);
  or or_3 (or_3_out, CReset, and_6_out);
  J_K_Flip_Flop j_k_ff_3 (
    .J(CEnable), .K(CEnable), .clk(j_k_ff_4_qn), .Q(D5), .Qn(j_k_ff_3_qn), .preset(and_5_out),
    .reset(or_3_out));
  not not_3 (not_3_out, I5);
  and and_6 (and_6_out, CWrite, not_3_out, Clock);
  not not_4 (not_4_out, I4);
  and and_7 (and_7_out, CWrite, I4, Clock);
  and and_8 (and_8_out, CWrite, not_4_out, Clock);
  or or_4 (or_4_out, CReset, and_8_out);
  J_K_Flip_Flop j_k_ff_4 (
    .J(CEnable), .K(CEnable), .clk(j_k_ff_5_qn), .Q(D4), .Qn(j_k_ff_4_qn), .preset(and_7_out),
    .reset(or_4_out));
  and and_9 (and_9_out, CWrite, I3, Clock);
  or or_5 (or_5_out, CReset, and_11_out);
  J_K_Flip_Flop j_k_ff_5 (
    .J(CEnable), .K(CEnable), .clk(j_k_ff_6_qn), .Q(D3), .Qn(j_k_ff_5_qn), .preset(and_9_out),
    .reset(or_5_out));
  not not_5 (not_5_out, I3);
  and and_10 (and_10_out, CWrite, I2, Clock);
  and and_11 (and_11_out, CWrite, not_5_out, Clock);
  J_K_Flip_Flop j_k_ff_6 (
    .J(CEnable), .K(CEnable), .clk(j_k_ff_7_qn), .Q(D2), .Qn(j_k_ff_6_qn), .preset(and_10_out),
    .reset(or_6_out));
  not not_6 (not_6_out, I2);
  and and_12 (and_12_out, CWrite, not_6_out, Clock);
  or or_6 (or_6_out, CReset, and_12_out);
  and and_13 (and_13_out, CWrite, I1, Clock);
  or or_7 (or_7_out, CReset, and_14_out);
  J_K_Flip_Flop j_k_ff_7 (
    .J(CEnable), .K(CEnable), .clk(j_k_ff_8_qn), .Q(D1), .Qn(j_k_ff_7_qn), .preset(and_13_out),
    .reset(or_7_out));
  not not_7 (not_7_out, I1);
  and and_14 (and_14_out, CWrite, not_7_out, Clock);
  and and_15 (and_15_out, CWrite, I0, Clock);
  J_K_Flip_Flop j_k_ff_8 (
    .J(CEnable), .K(CEnable), .clk(Clock), .Q(D0), .Qn(j_k_ff_8_qn), .preset(and_15_out), .reset(or_8_out));
  not not_8 (not_8_out, I0);
  and and_16 (and_16_out, CWrite, not_8_out, Clock);
  or or_8 (or_8_out, CReset, and_16_out);
  assign O7 = COut ? D7 : 1'bz;  // Controlled_Buffer controlled_buffer_1
  assign O6 = COut ? D6 : 1'bz;  // Controlled_Buffer controlled_buffer_2
  assign O5 = COut ? D5 : 1'bz;  // Controlled_Buffer controlled_buffer_3
  assign O4 = COut ? D4 : 1'bz;  // Controlled_Buffer controlled_buffer_4
  assign O3 = COut ? D3 : 1'bz;  // Controlled_Buffer controlled_buffer_5
  assign O2 = COut ? D2 : 1'bz;  // Controlled_Buffer controlled_buffer_6
  assign O1 = COut ? D1 : 1'bz;  // Controlled_Buffer controlled_buffer_7
  assign O0 = COut ? D0 : 1'bz;  // Controlled_Buffer controlled_buffer_8
endmodule

module pcloader (
  input  in_1,
  input  Reset,
  input  Enable,
  input  [7:0] ROM_data,
  input  in_5,
  input  Clock,
  output [7:0] ROM_addr,
  output RAM_write,
  output Addr_write,
  output Programming,
  output D7,
  output D6,
  output D5,
  output D4,
  output D3,
  output D2,
  output D1,
  output D0
);

  wire j_k_ff_1_q, j_k_ff_1_qn;
  wire [7:0] controlled_buffer_1_out;

  J_K_Flip_Flop j_k_ff_1 (
    .J(Clock), .K(Clock), .clk(Clock), .Q(j_k_ff_1_q), .Qn(j_k_ff_1_qn), .preset(in_5), .reset(in_5));
  assign controlled_buffer_1_out = j_k_ff_1_q ? ROM_data : 8'bz;  // Controlled_Buffer controlled_buffer_1
  assign D7 = Enable ? controlled_buffer_1_out[7] : 1'bz;  // Controlled_Buffer controlled_buffer_2
  assign D6 = Enable ? controlled_buffer_1_out[6] : 1'bz;  // Controlled_Buffer controlled_buffer_3
  assign D5 = Enable ? controlled_buffer_1_out[5] : 1'bz;  // Controlled_Buffer controlled_buffer_4
  assign D4 = Enable ? controlled_buffer_1_out[4] : 1'bz;  // Controlled_Buffer controlled_buffer_5
  assign D3 = Enable ? controlled_buffer_1_out[3] : 1'bz;  // Controlled_Buffer controlled_buffer_6
  assign D2 = Enable ? controlled_buffer_1_out[2] : 1'bz;  // Controlled_Buffer controlled_buffer_7
  counterr counterr_1 (
    .Clock(j_k_ff_1_qn), .COut(Enable), .CEnable(Enable), .CWrite(in_1), .CReset(Reset), .O7(ROM_addr[7]),
    .O6(ROM_addr[6]), .O5(ROM_addr[5]), .O4(ROM_addr[4]), .O3(ROM_addr[3]), .O2(ROM_addr[2]),
    .O1(ROM_addr[1]), .O0(ROM_addr[0]));  // open: I7, I6, I5, I4, I3, I2, I1, I0, D7, D6, D5, D4, D3, D2, D1, D0
  assign controlled_buffer_1_out = j_k_ff_1_qn ? ROM_addr : 8'bz;  // Controlled_Buffer controlled_buffer_8
  assign D1 = Enable ? controlled_buffer_1_out[1] : 1'bz;  // Controlled_Buffer controlled_buffer_9
  assign D0 = Enable ? controlled_buffer_1_out[0] : 1'bz;  // Controlled_Buffer controlled_buffer_10
  and and_1 (Addr_write, j_k_ff_1_qn, Enable);
  and and_2 (RAM_write, j_k_ff_1_q, Enable);

  assign Programming = Enable;
endmodule
