// Logisim project computer_8bits.circ as structural Verilog: 14 circuits, main circuit Processor
module Processor (
  input  Programming_mode
);

  wire alu_8_bits_1_cf, alu_8_bits_1_s0, alu_8_bits_1_s1, alu_8_bits_1_s2, alu_8_bits_1_s3, alu_8_bits_1_s4,
       alu_8_bits_1_s5, alu_8_bits_1_s6, alu_8_bits_1_s7, alu_8_bits_1_zf, and_1_out, clock_1_out,
       counter_8_bits_1_o0, counter_8_bits_1_o1, counter_8_bits_1_o2, counter_8_bits_1_o3,
       counter_8_bits_1_o4, counter_8_bits_1_o5, counter_8_bits_1_o6, counter_8_bits_1_o7,
       decoder_8_bits_to_7_segment_1_a1, decoder_8_bits_to_7_segment_1_a2, decoder_8_bits_to_7_segment_1_a3,
       decoder_8_bits_to_7_segment_1_b1, decoder_8_bits_to_7_segment_1_b2, decoder_8_bits_to_7_segment_1_b3,
       decoder_8_bits_to_7_segment_1_c1, decoder_8_bits_to_7_segment_1_c2, decoder_8_bits_to_7_segment_1_c3,
       decoder_8_bits_to_7_segment_1_d1, decoder_8_bits_to_7_segment_1_d2, decoder_8_bits_to_7_segment_1_d3,
       decoder_8_bits_to_7_segment_1_e1, decoder_8_bits_to_7_segment_1_e2, decoder_8_bits_to_7_segment_1_e3,
       decoder_8_bits_to_7_segment_1_f1, decoder_8_bits_to_7_segment_1_f2, decoder_8_bits_to_7_segment_1_f3,
       decoder_8_bits_to_7_segment_1_g1, decoder_8_bits_to_7_segment_1_g2, decoder_8_bits_to_7_segment_1_g3,
       instruction_decoder_1_ai, instruction_decoder_1_ao, instruction_decoder_1_bi,
       instruction_decoder_1_bo, instruction_decoder_1_ce, instruction_decoder_1_co,
       instruction_decoder_1_eo, instruction_decoder_1_fi, instruction_decoder_1_hl,
       instruction_decoder_1_ii, instruction_decoder_1_ir, instruction_decoder_1_jp,
       instruction_decoder_1_mi, instruction_decoder_1_oi, instruction_decoder_1_rr,
       instruction_decoder_1_rw, instruction_decoder_1_s0, instruction_decoder_1_s1,
       instruction_decoder_1_s2, instruction_decoder_1_s3, instruction_decoder_1_s4,
       instruction_decoder_1_s5, instruction_decoder_1_s6, instruction_decoder_1_s7,
       instruction_decoder_1_su, or_1_out, or_2_out, program_loader_1_addr_write,
       program_loader_1_programing, program_loader_1_ram_write, register_2_bits_1_b0, register_2_bits_1_b1,
       register_2_bits_1_o0, register_2_bits_1_o1, register_8_bits_1_b0, register_8_bits_1_b1,
       register_8_bits_1_b2, register_8_bits_1_b3, register_8_bits_1_b4, register_8_bits_1_b5,
       register_8_bits_1_b6, register_8_bits_1_b7, register_8_bits_1_o1, register_8_bits_1_o2,
       register_8_bits_1_o3, register_8_bits_1_o4, register_8_bits_1_o5, register_8_bits_1_o6,
       register_8_bits_1_o7, register_8_bits_2_b0, register_8_bits_2_b1, register_8_bits_2_b2,
       register_8_bits_2_b3, register_8_bits_2_b4, register_8_bits_2_b5, register_8_bits_2_b6,
       register_8_bits_2_b7, register_8_bits_2_o0, register_8_bits_2_o1, register_8_bits_2_o2,
       register_8_bits_2_o3, register_8_bits_2_o4, register_8_bits_3_b0, register_8_bits_3_b1,
       register_8_bits_3_b2, register_8_bits_3_b3, register_8_bits_3_b4, register_8_bits_3_b5,
       register_8_bits_3_b6, register_8_bits_3_b7, register_8_bits_4_o0, register_8_bits_4_o1,
       register_8_bits_4_o2, register_8_bits_4_o3, register_8_bits_4_o4, register_8_bits_4_o5,
       register_8_bits_4_o6, register_8_bits_4_o7, register_8_bits_5_o0, register_8_bits_5_o1,
       register_8_bits_5_o2, register_8_bits_5_o3, register_8_bits_5_o4, register_8_bits_5_o5,
       register_8_bits_5_o6, register_8_bits_5_o7, Reset_out, Reset_Ram_out, reverser_8_bits_1_o0,
       reverser_8_bits_1_o1, reverser_8_bits_1_o2, reverser_8_bits_1_o3, reverser_8_bits_1_o4,
       reverser_8_bits_1_o5, reverser_8_bits_1_o6, reverser_8_bits_1_o7;
  wire [3:0] register_8_bits_4_b0, register_8_bits_4_b4, sram_256_bytes_1_out_32, sram_256_bytes_1_out_36;
  wire [7:0] program_loader_1_rom_addr, rom_1_data;

  DotMatrix #(.dotshape("circle"), .matrixcols(8), .matrixrows(1)) dotmatrix_1 (
    .col0(instruction_decoder_1_s7), .col1(instruction_decoder_1_s6), .col2(instruction_decoder_1_s5),
    .col3(instruction_decoder_1_s4), .col4(instruction_decoder_1_s3), .col5(instruction_decoder_1_s2),
    .col6(instruction_decoder_1_s1), .col7(instruction_decoder_1_s0));
  DotMatrix #(.dotshape("circle"), .matrixcols(8), .matrixrows(1)) dotmatrix_2 (
    .col0(register_8_bits_1_b7), .col1(register_8_bits_1_b6), .col2(register_8_bits_1_b5),
    .col3(register_8_bits_1_b4), .col4(register_8_bits_1_b3), .col5(register_8_bits_1_b2),
    .col6(register_8_bits_1_b1), .col7(register_8_bits_1_b0));
  LED led_1 (.in(instruction_decoder_1_ir));
  Register_8_bits register_8_bits_1 (
    .I7(register_8_bits_1_o7), .I6(register_8_bits_1_o6), .I5(register_8_bits_1_o5),
    .I4(register_8_bits_1_o4), .I3(register_8_bits_1_o3), .I2(register_8_bits_1_o2),
    .I1(register_8_bits_1_o1), .I0(register_8_bits_1_o6), .Clock(and_1_out), .Load(instruction_decoder_1_ai),
    .Reset(Reset_out), .Enable(instruction_decoder_1_ao), .B7(register_8_bits_1_b7),
    .B6(register_8_bits_1_b6), .B5(register_8_bits_1_b5), .B4(register_8_bits_1_b4),
    .B3(register_8_bits_1_b3), .B2(register_8_bits_1_b2), .B1(register_8_bits_1_b1),
    .B0(register_8_bits_1_b0), .O7(register_8_bits_1_o7), .O6(register_8_bits_1_o6),
    .O5(register_8_bits_1_o5), .O4(register_8_bits_1_o4), .O3(register_8_bits_1_o3),
    .O2(register_8_bits_1_o2), .O1(register_8_bits_1_o1), .O0(register_8_bits_1_o6));
  DotMatrix #(.dotshape("circle"), .matrixcols(8), .matrixrows(1)) dotmatrix_3 (
    .col0(alu_8_bits_1_s7), .col1(alu_8_bits_1_s6), .col2(alu_8_bits_1_s5), .col3(alu_8_bits_1_s4),
    .col4(alu_8_bits_1_s3), .col5(alu_8_bits_1_s2), .col6(alu_8_bits_1_s1), .col7(alu_8_bits_1_s0));
  DotMatrix #(.dotshape("circle"), .matrixcols(8), .matrixrows(1)) dotmatrix_4 (
    .col0(reverser_8_bits_1_o0), .col1(reverser_8_bits_1_o1), .col2(reverser_8_bits_1_o2),
    .col3(reverser_8_bits_1_o3), .col4(reverser_8_bits_1_o4), .col5(reverser_8_bits_1_o5),
    .col6(reverser_8_bits_1_o6), .col7(reverser_8_bits_1_o7));
  Reverser_8_bits reverser_8_bits_1 (
    .I5(register_8_bits_2_b2), .I4(register_8_bits_2_b3), .I3(register_8_bits_2_b4),
    .I2(register_8_bits_2_b5), .I1(register_8_bits_2_b6), .I0(register_8_bits_2_b7),
    .I7(register_8_bits_2_b0), .I6(register_8_bits_2_b1), .O2(reverser_8_bits_1_o2),
    .O3(reverser_8_bits_1_o3), .O4(reverser_8_bits_1_o4), .O5(reverser_8_bits_1_o5),
    .O6(reverser_8_bits_1_o6), .O7(reverser_8_bits_1_o7), .O0(reverser_8_bits_1_o0), .O1(reverser_8_bits_1_o1));
  DotMatrix #(.dotshape("circle"), .inputtype("row"), .matrixcols(1), .matrixrows(5)) dotmatrix_5 (
    .row0(register_8_bits_2_o0), .row1(register_8_bits_2_o1), .row2(register_8_bits_2_o2),
    .row3(register_8_bits_2_o3), .row4(register_8_bits_2_o4));
  Instruction_decoder instruction_decoder_1 (
    .OP0(register_8_bits_2_o0), .OP1(register_8_bits_2_o1), .OP2(register_8_bits_2_o2),
    .OP3(register_8_bits_2_o3), .OP4(register_8_bits_2_o4), .PM(Programming_mode), .Clear(Reset_out),
    .CLK(and_1_out), .ZF(register_2_bits_1_o0), .CF(register_2_bits_1_o1), .JP(instruction_decoder_1_jp),
    .CO(instruction_decoder_1_co), .CE(instruction_decoder_1_ce), .IR(instruction_decoder_1_ir),
    .II(instruction_decoder_1_ii), .RR(instruction_decoder_1_rr), .RW(instruction_decoder_1_rw),
    .MI(instruction_decoder_1_mi), .BO(instruction_decoder_1_bo), .BI(instruction_decoder_1_bi),
    .SU(instruction_decoder_1_su), .EO(instruction_decoder_1_eo), .AO(instruction_decoder_1_ao),
    .AI(instruction_decoder_1_ai), .HL(instruction_decoder_1_hl), .FI(instruction_decoder_1_fi),
    .OI(instruction_decoder_1_oi), .S7(instruction_decoder_1_s7), .S6(instruction_decoder_1_s6),
    .S5(instruction_decoder_1_s5), .S4(instruction_decoder_1_s4), .S3(instruction_decoder_1_s3),
    .S2(instruction_decoder_1_s2), .S1(instruction_decoder_1_s1), .S0(instruction_decoder_1_s0));
  Register_8_bits register_8_bits_2 (
    .I7(register_8_bits_1_o7), .I6(register_8_bits_1_o6), .I5(register_8_bits_1_o5),
    .I4(register_8_bits_1_o4), .I3(register_8_bits_1_o3), .I2(register_8_bits_1_o2),
    .I1(register_8_bits_1_o1), .I0(register_8_bits_1_o6), .Clock(and_1_out), .Load(instruction_decoder_1_ii),
    .Reset(Reset_out), .Enable(1'b1), .B7(register_8_bits_2_b7), .B6(register_8_bits_2_b6),
    .B5(register_8_bits_2_b5), .B4(register_8_bits_2_b4), .B3(register_8_bits_2_b3),
    .B2(register_8_bits_2_b2), .B1(register_8_bits_2_b1), .B0(register_8_bits_2_b0),
    .O4(register_8_bits_2_o4), .O3(register_8_bits_2_o3), .O2(register_8_bits_2_o2),
    .O1(register_8_bits_2_o1), .O0(register_8_bits_2_o0));  // open: O7, O6, O5
  Register_2_bits register_2_bits_1 (
    .Load(instruction_decoder_1_fi), .Reset(Reset_out), .Enable(1'b1), .I1(alu_8_bits_1_cf),
    .I0(alu_8_bits_1_zf), .Clock(and_1_out), .B1(register_2_bits_1_b1), .B0(register_2_bits_1_b0),
    .O1(register_2_bits_1_o1), .O0(register_2_bits_1_o0));
  DotMatrix #(.dotshape("circle"), .matrixcols(2), .matrixrows(1)) dotmatrix_6 (
    .col0(register_2_bits_1_b1), .col1(register_2_bits_1_b0));
  ALU_8_bits alu_8_bits_1 (
    .B7(register_8_bits_3_b7), .A7(register_8_bits_1_b7), .B6(register_8_bits_3_b6),
    .A6(register_8_bits_1_b6), .B5(register_8_bits_3_b5), .A5(register_8_bits_1_b5),
    .B4(register_8_bits_3_b4), .A4(register_8_bits_1_b4), .B3(register_8_bits_3_b3),
    .A3(register_8_bits_1_b3), .B2(register_8_bits_3_b2), .A2(register_8_bits_1_b2),
    .Su(instruction_decoder_1_su), .B1(register_8_bits_3_b1), .A1(register_8_bits_1_b1),
    .B0(register_8_bits_3_b0), .A0(register_8_bits_1_b0), .En(instruction_decoder_1_eo),
    .CF(alu_8_bits_1_cf), .ZF(alu_8_bits_1_zf), .S7(alu_8_bits_1_s7), .S6(alu_8_bits_1_s6),
    .S5(alu_8_bits_1_s5), .S4(alu_8_bits_1_s4), .S3(alu_8_bits_1_s3), .S2(alu_8_bits_1_s2),
    .S1(alu_8_bits_1_s1), .S0(alu_8_bits_1_s0), .E7(register_8_bits_1_o7), .E6(register_8_bits_1_o6),
    .E5(register_8_bits_1_o5), .E4(register_8_bits_1_o4), .E3(register_8_bits_1_o3),
    .E2(register_8_bits_1_o2), .E1(register_8_bits_1_o1), .E0(register_8_bits_1_o6));
  DotMatrix #(.dotshape("circle"), .inputtype("row"), .matrixcols(1), .matrixrows(8)) dotmatrix_7 (
    .row0(counter_8_bits_1_o7), .row1(counter_8_bits_1_o6), .row2(counter_8_bits_1_o5),
    .row3(counter_8_bits_1_o4), .row4(counter_8_bits_1_o3), .row5(counter_8_bits_1_o2),
    .row6(counter_8_bits_1_o1), .row7(counter_8_bits_1_o0));
  DotMatrix #(.dotshape("circle"), .matrixcols(8), .matrixrows(1)) dotmatrix_8 (
    .col0(register_8_bits_3_b7), .col1(register_8_bits_3_b6), .col2(register_8_bits_3_b5),
    .col3(register_8_bits_3_b4), .col4(register_8_bits_3_b3), .col5(register_8_bits_3_b2),
    .col6(register_8_bits_3_b1), .col7(register_8_bits_3_b0));
  Register_8_bits register_8_bits_3 (
    .I7(register_8_bits_1_o7), .I6(register_8_bits_1_o6), .I5(register_8_bits_1_o5),
    .I4(register_8_bits_1_o4), .I3(register_8_bits_1_o3), .I2(register_8_bits_1_o2),
    .I1(register_8_bits_1_o1), .I0(register_8_bits_1_o6), .Clock(and_1_out), .Load(instruction_decoder_1_bi),
    .Reset(Reset_out), .Enable(instruction_decoder_1_bo), .B7(register_8_bits_3_b7),
    .B6(register_8_bits_3_b6), .B5(register_8_bits_3_b5), .B4(register_8_bits_3_b4),
    .B3(register_8_bits_3_b3), .B2(register_8_bits_3_b2), .B1(register_8_bits_3_b1),
    .B0(register_8_bits_3_b0), .O7(register_8_bits_1_o7), .O6(register_8_bits_1_o6),
    .O5(register_8_bits_1_o5), .O4(register_8_bits_1_o4), .O3(register_8_bits_1_o3),
    .O2(register_8_bits_1_o2), .O1(register_8_bits_1_o1), .O0(register_8_bits_1_o6));
  Counter_8_bits counter_8_bits_1 (
    .CEnable(instruction_decoder_1_ce), .CWrite(instruction_decoder_1_jp), .CReset(Reset_out),
    .Clock(and_1_out), .I7(register_8_bits_1_o7), .I6(register_8_bits_1_o6), .I5(register_8_bits_1_o5),
    .I4(register_8_bits_1_o4), .I3(register_8_bits_1_o3), .I2(register_8_bits_1_o2),
    .I1(register_8_bits_1_o1), .I0(register_8_bits_1_o6), .O7(counter_8_bits_1_o7), .O6(counter_8_bits_1_o6),
    .O5(counter_8_bits_1_o5), .O4(counter_8_bits_1_o4), .O3(counter_8_bits_1_o3), .O2(counter_8_bits_1_o2),
    .O1(counter_8_bits_1_o1), .O0(counter_8_bits_1_o0));
  or or_1 (or_1_out, instruction_decoder_1_mi, program_loader_1_addr_write);
  DotMatrix #(.dotshape("circle"), .matrixcols(8), .matrixrows(1)) dotmatrix_9 (
    .col0(register_8_bits_4_b4[3]), .col1(register_8_bits_4_b4[2]), .col2(register_8_bits_4_b4[1]),
    .col3(register_8_bits_4_b4[0]), .col4(register_8_bits_4_b0[3]), .col5(register_8_bits_4_b0[2]),
    .col6(register_8_bits_4_b0[1]), .col7(register_8_bits_4_b0[0]));
  Hex_Digit_Display #(.decimalPoint("false")) hex_digit_display_1 (.value(register_8_bits_4_b4));
  Register_8_bits register_8_bits_4 (
    .I7(register_8_bits_1_o7), .I6(register_8_bits_1_o6), .I5(register_8_bits_1_o5),
    .I4(register_8_bits_1_o4), .I3(register_8_bits_1_o3), .I2(register_8_bits_1_o2),
    .I1(register_8_bits_1_o1), .I0(register_8_bits_1_o6), .Clock(and_1_out), .Load(or_1_out),
    .Reset(Reset_out), .Enable(1'b1), .B7(register_8_bits_4_b4[3]), .B6(register_8_bits_4_b4[2]),
    .B5(register_8_bits_4_b4[1]), .B4(register_8_bits_4_b4[0]), .B3(register_8_bits_4_b0[3]),
    .B2(register_8_bits_4_b0[2]), .B1(register_8_bits_4_b0[1]), .B0(register_8_bits_4_b0[0]),
    .O7(register_8_bits_4_o7), .O6(register_8_bits_4_o6), .O5(register_8_bits_4_o5),
    .O4(register_8_bits_4_o4), .O3(register_8_bits_4_o3), .O2(register_8_bits_4_o2),
    .O1(register_8_bits_4_o1), .O0(register_8_bits_4_o0));
  Hex_Digit_Display #(.decimalPoint("false")) hex_digit_display_2 (.value(register_8_bits_4_b0));
  Hex_Digit_Display #(.decimalPoint("false")) hex_digit_display_3 (.value(sram_256_bytes_1_out_32));
  Hex_Digit_Display #(.decimalPoint("false")) hex_digit_display_4 (.value(sram_256_bytes_1_out_36));
  Register_8_bits register_8_bits_5 (
    .I7(register_8_bits_1_o7), .I6(register_8_bits_1_o6), .I5(register_8_bits_1_o5),
    .I4(register_8_bits_1_o4), .I3(register_8_bits_1_o3), .I2(register_8_bits_1_o2),
    .I1(register_8_bits_1_o1), .I0(register_8_bits_1_o6), .Clock(and_1_out), .Load(instruction_decoder_1_oi),
    .Reset(Reset_out), .Enable(1'b1), .O7(register_8_bits_5_o7), .O6(register_8_bits_5_o6),
    .O5(register_8_bits_5_o5), .O4(register_8_bits_5_o4), .O3(register_8_bits_5_o3),
    .O2(register_8_bits_5_o2), .O1(register_8_bits_5_o1), .O0(register_8_bits_5_o0));  // open: B7, B6, B5, B4, B3, B2, B1, B0
  _7_Segment_Display u_7_segment_display_1 (
    .g(decoder_8_bits_to_7_segment_1_g3), .f(decoder_8_bits_to_7_segment_1_f3),
    .a(decoder_8_bits_to_7_segment_1_a3), .b(decoder_8_bits_to_7_segment_1_b3),
    .e(decoder_8_bits_to_7_segment_1_e3), .d(decoder_8_bits_to_7_segment_1_d3),
    .c(decoder_8_bits_to_7_segment_1_c3));  // open: dp
  _7_Segment_Display u_7_segment_display_2 (
    .g(decoder_8_bits_to_7_segment_1_g2), .f(decoder_8_bits_to_7_segment_1_f2),
    .a(decoder_8_bits_to_7_segment_1_a2), .b(decoder_8_bits_to_7_segment_1_b2),
    .e(decoder_8_bits_to_7_segment_1_e2), .d(decoder_8_bits_to_7_segment_1_d2),
    .c(decoder_8_bits_to_7_segment_1_c2));  // open: dp
  or or_2 (or_2_out, instruction_decoder_1_rw, program_loader_1_ram_write);
  SRAM_256_bytes sram_256_bytes_1 (
    .D7(register_8_bits_1_o7), .D6(register_8_bits_1_o6), .D5(register_8_bits_1_o5),
    .D4(register_8_bits_1_o4), .D3(register_8_bits_1_o3), .D2(register_8_bits_1_o2),
    .D1(register_8_bits_1_o1), .D0(register_8_bits_1_o6), .Write(or_2_out), .A7(register_8_bits_4_o7),
    .A6(register_8_bits_4_o6), .A5(register_8_bits_4_o5), .A4(register_8_bits_4_o4),
    .A3(register_8_bits_4_o3), .A2(register_8_bits_4_o2), .A1(register_8_bits_4_o1),
    .A0(register_8_bits_4_o0), .Read(instruction_decoder_1_rr), .Clock(and_1_out), .Clear(Reset_Ram_out),
    .out_29(sram_256_bytes_1_out_32[3]), .out_30(sram_256_bytes_1_out_32[2]),
    .out_31(sram_256_bytes_1_out_32[1]), .out_32(sram_256_bytes_1_out_32[0]),
    .out_33(sram_256_bytes_1_out_36[3]), .out_34(sram_256_bytes_1_out_36[2]),
    .out_35(sram_256_bytes_1_out_36[1]), .out_36(sram_256_bytes_1_out_36[0]), .O7(register_8_bits_1_o7),
    .O6(register_8_bits_1_o6), .O5(register_8_bits_1_o5), .O4(register_8_bits_1_o4),
    .O3(register_8_bits_1_o3), .O2(register_8_bits_1_o2), .O1(register_8_bits_1_o1), .O0(register_8_bits_1_o6));
  DotMatrix #(.dotshape("circle"), .inputtype("row"), .matrixcols(1), .matrixrows(8)) dotmatrix_10 (
    .row0(register_8_bits_1_o7), .row1(register_8_bits_1_o6), .row2(register_8_bits_1_o5),
    .row3(register_8_bits_1_o4), .row4(register_8_bits_1_o3), .row5(register_8_bits_1_o2),
    .row6(register_8_bits_1_o1), .row7(register_8_bits_1_o6));
  _7_Segment_Display u_7_segment_display_3 (
    .g(decoder_8_bits_to_7_segment_1_g1), .f(decoder_8_bits_to_7_segment_1_f1),
    .a(decoder_8_bits_to_7_segment_1_a1), .b(decoder_8_bits_to_7_segment_1_b1),
    .e(decoder_8_bits_to_7_segment_1_e1), .d(decoder_8_bits_to_7_segment_1_d1),
    .c(decoder_8_bits_to_7_segment_1_c1));  // open: dp
  Decoder_8_bits_to_7_segment decoder_8_bits_to_7_segment_1 (
    .I2(register_8_bits_5_o2), .I3(register_8_bits_5_o3), .I4(register_8_bits_5_o4),
    .I5(register_8_bits_5_o5), .I6(register_8_bits_5_o6), .I7(register_8_bits_5_o7),
    .I0(register_8_bits_5_o0), .I1(register_8_bits_5_o1), .d1(decoder_8_bits_to_7_segment_1_d1),
    .e1(decoder_8_bits_to_7_segment_1_e1), .f1(decoder_8_bits_to_7_segment_1_f1),
    .g1(decoder_8_bits_to_7_segment_1_g1), .a2(decoder_8_bits_to_7_segment_1_a2),
    .b2(decoder_8_bits_to_7_segment_1_b2), .c2(decoder_8_bits_to_7_segment_1_c2),
    .d2(decoder_8_bits_to_7_segment_1_d2), .e2(decoder_8_bits_to_7_segment_1_e2),
    .f2(decoder_8_bits_to_7_segment_1_f2), .g2(decoder_8_bits_to_7_segment_1_g2),
    .a3(decoder_8_bits_to_7_segment_1_a3), .b3(decoder_8_bits_to_7_segment_1_b3),
    .c3(decoder_8_bits_to_7_segment_1_c3), .d3(decoder_8_bits_to_7_segment_1_d3),
    .e3(decoder_8_bits_to_7_segment_1_e3), .f3(decoder_8_bits_to_7_segment_1_f3),
    .g3(decoder_8_bits_to_7_segment_1_g3), .a1(decoder_8_bits_to_7_segment_1_a1),
    .b1(decoder_8_bits_to_7_segment_1_b1), .c1(decoder_8_bits_to_7_segment_1_c1));
  ROM rom_1 (.addr(program_loader_1_rom_addr), .data(rom_1_data));
  Program_loader program_loader_1 (
    .ROM_data(rom_1_data), .Clock(and_1_out), .Reset(Reset_out), .Enabled(Programming_mode),
    .ROM_addr(program_loader_1_rom_addr), .O5(register_8_bits_1_o5), .O4(register_8_bits_1_o4),
    .O3(register_8_bits_1_o3), .O2(register_8_bits_1_o2), .O1(register_8_bits_1_o1),
    .O0(register_8_bits_1_o6), .Programing(program_loader_1_programing),
    .Addr_write(program_loader_1_addr_write), .RAM_write(program_loader_1_ram_write),
    .O7(register_8_bits_1_o7), .O6(register_8_bits_1_o6));
  Button Reset (.out(Reset_out));
  Button Reset_Ram (.out(Reset_Ram_out));
  LED Programming (.in(program_loader_1_programing));
  Clock clock_1 (.out(clock_1_out));
  and and_1 (and_1_out, ~instruction_decoder_1_hl, clock_1_out, ~Reset_out);  // AND_Gate

  // Notes on the sheet:
  //   Register A
  //   Instruction Decoder
  //   ALU
  //   Flags
  //   CF ZF
  //   Instruction
  //   Register
  //   Register B
  //   PC Register
  //   Memory
  //   Register
  //   Out
  //   Register
  //   contents of rom_1 (hex, n*v repeats v):
  //   2 0 4 18 f 18 2 1 4 19 f 19 3 18 9 19 7 18 4 19 12 0 10 a
endmodule

module Address_Decoder_4_bits (
  input  A3,
  input  Enable,
  input  A2,
  input  A1,
  input  A0,
  output DF,
  output DE,
  output DD,
  output DC,
  output DB,
  output DA,
  output D9,
  output D8,
  output D7,
  output D6,
  output D5,
  output D4,
  output D3,
  output D2,
  output D1,
  output D0
);

  wire and_1_out, and_2_out, and_3_out, and_4_out, and_5_out, and_6_out, and_7_out, and_8_out, and_9_out,
       and_10_out, and_11_out, and_12_out, and_13_out, and_14_out, and_15_out, and_16_out, not_1_out,
       not_2_out, not_3_out, not_4_out;

  not not_1 (not_1_out, A3);
  not not_2 (not_2_out, A2);
  not not_3 (not_3_out, A1);
  not not_4 (not_4_out, A0);
  assign DF = Enable ? and_16_out : 1'bz;  // Controlled_Buffer controlled_buffer_1
  assign DE = Enable ? and_15_out : 1'bz;  // Controlled_Buffer controlled_buffer_2
  and and_1 (and_1_out, not_1_out, not_2_out, not_3_out, not_4_out);
  and and_2 (and_2_out, not_1_out, not_2_out, not_3_out, A0);
  and and_3 (and_3_out, not_1_out, not_2_out, A1, not_4_out);
  and and_4 (and_4_out, not_1_out, not_2_out, A1, A0);
  and and_5 (and_5_out, not_1_out, A2, not_3_out, not_4_out);
  and and_6 (and_6_out, not_1_out, A2, not_3_out, A0);
  and and_7 (and_7_out, not_1_out, A2, A1, not_4_out);
  and and_8 (and_8_out, not_1_out, A2, A1, A0);
  and and_9 (and_9_out, A3, not_2_out, not_3_out, not_4_out);
  and and_10 (and_10_out, A3, not_2_out, not_3_out, A0);
  and and_11 (and_11_out, A3, not_2_out, A1, not_4_out);
  and and_12 (and_12_out, A3, not_2_out, A1, A0);
  and and_13 (and_13_out, A3, A2, not_3_out, not_4_out);
  and and_14 (and_14_out, A3, A2, not_3_out, A0);
  and and_15 (and_15_out, A3, A2, A1, not_4_out);
  and and_16 (and_16_out, A3, A2, A1, A0);
  assign DD = Enable ? and_14_out : 1'bz;  // Controlled_Buffer controlled_buffer_3
  assign DC = Enable ? and_13_out : 1'bz;  // Controlled_Buffer controlled_buffer_4
  assign DB = Enable ? and_12_out : 1'bz;  // Controlled_Buffer controlled_buffer_5
  assign DA = Enable ? and_11_out : 1'bz;  // Controlled_Buffer controlled_buffer_6
  assign D9 = Enable ? and_10_out : 1'bz;  // Controlled_Buffer controlled_buffer_7
  assign D8 = Enable ? and_9_out : 1'bz;  // Controlled_Buffer controlled_buffer_8
  assign D7 = Enable ? and_8_out : 1'bz;  // Controlled_Buffer controlled_buffer_9
  assign D6 = Enable ? and_7_out : 1'bz;  // Controlled_Buffer controlled_buffer_10
  assign D5 = Enable ? and_6_out : 1'bz;  // Controlled_Buffer controlled_buffer_11
  assign D4 = Enable ? and_5_out : 1'bz;  // Controlled_Buffer controlled_buffer_12
  assign D3 = Enable ? and_4_out : 1'bz;  // Controlled_Buffer controlled_buffer_13
  assign D2 = Enable ? and_3_out : 1'bz;  // Controlled_Buffer controlled_buffer_14
  assign D1 = Enable ? and_2_out : 1'bz;  // Controlled_Buffer controlled_buffer_15
  assign D0 = Enable ? and_1_out : 1'bz;  // Controlled_Buffer controlled_buffer_16
endmodule

module ALU_8_bits (
  input  Su,
  input  A7,
  input  A6,
  input  A5,
  input  A4,
  input  A3,
  input  A2,
  input  A1,
  input  A0,
  input  En,
  input  B7,
  input  B6,
  input  B5,
  input  B4,
  input  B3,
  input  B2,
  input  B1,
  input  B0,
  output CF,
  output ZF,
  output S7,
  output S6,
  output S5,
  output S4,
  output S3,
  output S2,
  output S1,
  output S0,
  output E7,
  output E6,
  output E5,
  output E4,
  output E3,
  output E2,
  output E1,
  output E0
);

  wire full_adder_1_co, full_adder_2_co, full_adder_3_co, full_adder_4_co, full_adder_5_co, full_adder_6_co,
       full_adder_7_co, xor_1_out, xor_2_out, xor_3_out, xor_4_out, xor_5_out, xor_6_out, xor_7_out,
       xor_8_out;

  Full_adder full_adder_1 (.A(A1), .B(xor_7_out), .Ci(full_adder_2_co), .Co(full_adder_1_co), .E(S1));
  Full_adder full_adder_2 (.A(A0), .B(xor_8_out), .Ci(Su), .Co(full_adder_2_co), .E(S0));
  xor xor_1 (xor_1_out, Su, B7);
  Full_adder full_adder_3 (.A(A2), .B(xor_6_out), .Ci(full_adder_1_co), .Co(full_adder_3_co), .E(S2));
  xor xor_2 (xor_2_out, Su, B6);
  xor xor_3 (xor_3_out, Su, B5);
  Full_adder full_adder_4 (.A(A3), .B(xor_5_out), .Ci(full_adder_3_co), .Co(full_adder_4_co), .E(S3));
  xor xor_4 (xor_4_out, Su, B4);
  xor xor_5 (xor_5_out, Su, B3);
  Full_adder full_adder_5 (.A(A4), .B(xor_4_out), .Ci(full_adder_4_co), .Co(full_adder_5_co), .E(S4));
  Full_adder full_adder_6 (.A(A5), .B(xor_3_out), .Ci(full_adder_5_co), .Co(full_adder_6_co), .E(S5));
  xor xor_6 (xor_6_out, Su, B2);
  xor xor_7 (xor_7_out, Su, B1);
  Full_adder full_adder_7 (.A(A6), .B(xor_2_out), .Ci(full_adder_6_co), .Co(full_adder_7_co), .E(S6));
  xor xor_8 (xor_8_out, Su, B0);
  Full_adder full_adder_8 (.A(A7), .B(xor_1_out), .Ci(full_adder_7_co), .Co(CF), .E(S7));
  nor nor_1 (ZF, S7, S6, S5, S4, S3, S2, S1, S0);
  assign E7 = En ? S7 : 1'bz;  // Controlled_Buffer controlled_buffer_1
  assign E6 = En ? S6 : 1'bz;  // Controlled_Buffer controlled_buffer_2
  assign E5 = En ? S5 : 1'bz;  // Controlled_Buffer controlled_buffer_3
  assign E4 = En ? S4 : 1'bz;  // Controlled_Buffer controlled_buffer_4
  assign E3 = En ? S3 : 1'bz;  // Controlled_Buffer controlled_buffer_5
  assign E2 = En ? S2 : 1'bz;  // Controlled_Buffer controlled_buffer_6
  assign E1 = En ? S1 : 1'bz;  // Controlled_Buffer controlled_buffer_7
  assign E0 = En ? S0 : 1'bz;  // Controlled_Buffer controlled_buffer_8
endmodule

module Counter_8_bits (
  input  CEnable,
  input  CWrite,
  input  CReset,
  input  Clock,
  input  I7,
  input  I6,
  input  I5,
  input  I4,
  input  I3,
  input  I2,
  input  I1,
  input  I0,
  output O7,
  output O6,
  output O5,
  output O4,
  output O3,
  output O2,
  output O1,
  output O0
);

  wire and_1_out, and_2_out, and_3_out, and_4_out, and_5_out, and_6_out, and_7_out, and_8_out, and_9_out,
       and_10_out, and_11_out, and_12_out, and_13_out, and_14_out, and_15_out, and_16_out, and_17_out,
       j_k_ff_2_qn, j_k_ff_3_qn, j_k_ff_4_qn, j_k_ff_5_qn, j_k_ff_6_qn, j_k_ff_7_qn, j_k_ff_8_qn, or_1_out,
       or_2_out, or_3_out, or_4_out, or_5_out, or_6_out, or_7_out, or_8_out;

  and and_1 (and_1_out, CReset, Clock);
  J_K_Flip_Flop j_k_ff_1 (
    .J(CEnable), .K(CEnable), .clk(j_k_ff_2_qn), .Q(O7), .preset(and_2_out), .reset(or_1_out));  // open: Qn
  or or_1 (or_1_out, and_1_out, and_3_out);
  and and_2 (and_2_out, CWrite, I7, Clock);
  and and_3 (and_3_out, CWrite, ~I7, Clock);  // AND_Gate
  J_K_Flip_Flop j_k_ff_2 (
    .J(CEnable), .K(CEnable), .clk(j_k_ff_3_qn), .Q(O6), .Qn(j_k_ff_2_qn), .preset(and_4_out),
    .reset(or_2_out));
  or or_2 (or_2_out, and_1_out, and_5_out);
  and and_4 (and_4_out, CWrite, I6, Clock);
  J_K_Flip_Flop j_k_ff_3 (
    .J(CEnable), .K(CEnable), .clk(j_k_ff_4_qn), .Q(O5), .Qn(j_k_ff_3_qn), .preset(and_6_out),
    .reset(or_3_out));
  and and_5 (and_5_out, CWrite, ~I6, Clock);  // AND_Gate
  and and_6 (and_6_out, CWrite, I5, Clock);
  J_K_Flip_Flop j_k_ff_4 (
    .J(CEnable), .K(CEnable), .clk(j_k_ff_5_qn), .Q(O4), .Qn(j_k_ff_4_qn), .preset(and_8_out),
    .reset(or_4_out));
  or or_3 (or_3_out, and_1_out, and_7_out);
  and and_7 (and_7_out, CWrite, ~I5, Clock);  // AND_Gate
  and and_8 (and_8_out, CWrite, I4, Clock);
  or or_4 (or_4_out, and_1_out, and_9_out);
  and and_9 (and_9_out, CWrite, ~I4, Clock);  // AND_Gate
  and and_10 (and_10_out, CWrite, I3, Clock);
  J_K_Flip_Flop j_k_ff_5 (
    .J(CEnable), .K(CEnable), .clk(j_k_ff_6_qn), .Q(O3), .Qn(j_k_ff_5_qn), .preset(and_10_out),
    .reset(or_5_out));
  or or_5 (or_5_out, and_1_out, and_11_out);
  and and_11 (and_11_out, CWrite, ~I3, Clock);  // AND_Gate
  J_K_Flip_Flop j_k_ff_6 (
    .J(CEnable), .K(CEnable), .clk(j_k_ff_7_qn), .Q(O2), .Qn(j_k_ff_6_qn), .preset(and_12_out),
    .reset(or_6_out));
  or or_6 (or_6_out, and_1_out, and_13_out);
  and and_12 (and_12_out, CWrite, I2, Clock);
  and and_13 (and_13_out, CWrite, ~I2, Clock);  // AND_Gate
  J_K_Flip_Flop j_k_ff_7 (
    .J(CEnable), .K(CEnable), .clk(j_k_ff_8_qn), .Q(O1), .Qn(j_k_ff_7_qn), .preset(and_14_out),
    .reset(or_7_out));
  or or_7 (or_7_out, and_1_out, and_15_out);
  and and_14 (and_14_out, CWrite, I1, Clock);
  and and_15 (and_15_out, CWrite, ~I1, Clock);  // AND_Gate
  J_K_Flip_Flop j_k_ff_8 (
    .J(CEnable), .K(CEnable), .clk(Clock), .Q(O0), .Qn(j_k_ff_8_qn), .preset(and_16_out), .reset(or_8_out));
  or or_8 (or_8_out, and_1_out, and_17_out);
  and and_16 (and_16_out, CWrite, I0, Clock);
  and and_17 (and_17_out, CWrite, ~I0, Clock);  // AND_Gate
endmodule

module Full_adder (
  input  A,
  input  B,
  input  Ci,
  output E,
  output Co
);

  wire and_1_out, and_2_out, xor_1_out;

  xor xor_1 (xor_1_out, A, B);
  xor xor_2 (E, xor_1_out, Ci);
  and and_1 (and_1_out, xor_1_out, Ci);
  or or_1 (Co, and_1_out, and_2_out);
  and and_2 (and_2_out, A, B);
endmodule

module Grounder_4_bits (
  input  in_1,
  output G3,
  output G2,
  output G1,
  output G0
);

  assign G3 = in_1 ? 1'b0 : 1'bz;  // Controlled_Buffer controlled_buffer_1
  assign G1 = in_1 ? 1'b0 : 1'bz;  // Controlled_Buffer controlled_buffer_2
  assign G2 = in_1 ? 1'b0 : 1'bz;  // Controlled_Buffer controlled_buffer_3
  assign G0 = in_1 ? 1'b0 : 1'bz;  // Controlled_Buffer controlled_buffer_4
endmodule

module Register_8_bits (
  input  Clock,
  input  Load,
  input  Reset,
  input  Enable,
  input  I7,
  input  I6,
  input  I5,
  input  I4,
  input  I3,
  input  I2,
  input  I1,
  input  I0,
  output B7,
  output B6,
  output B5,
  output B4,
  output B3,
  output B2,
  output B1,
  output B0,
  output O7,
  output O6,
  output O5,
  output O4,
  output O3,
  output O2,
  output O1,
  output O0
);

  Register #(.width(1)) register_1 (.D(I7), .en(Load), .clk(Clock), .Q(B7), .clr(Reset));
  Register #(.width(1)) register_2 (.D(I6), .en(Load), .clk(Clock), .Q(B6), .clr(Reset));
  Register #(.width(1)) register_3 (.D(I5), .en(Load), .clk(Clock), .Q(B5), .clr(Reset));
  Register #(.width(1)) register_4 (.D(I4), .en(Load), .clk(Clock), .Q(B4), .clr(Reset));
  Register #(.width(1)) register_5 (.D(I3), .en(Load), .clk(Clock), .Q(B3), .clr(Reset));
  Register #(.width(1)) register_6 (.D(I2), .en(Load), .clk(Clock), .Q(B2), .clr(Reset));
  Register #(.width(1)) register_7 (.D(I1), .en(Load), .clk(Clock), .Q(B1), .clr(Reset));
  Register #(.width(1)) register_8 (.D(I0), .en(Load), .clk(Clock), .Q(B0), .clr(Reset));
  assign O7 = Enable ? B7 : 1'bz;  // Controlled_Buffer controlled_buffer_1
  assign O6 = Enable ? B6 : 1'bz;  // Controlled_Buffer controlled_buffer_2
  assign O5 = Enable ? B5 : 1'bz;  // Controlled_Buffer controlled_buffer_3
  assign O4 = Enable ? B4 : 1'bz;  // Controlled_Buffer controlled_buffer_4
  assign O3 = Enable ? B3 : 1'bz;  // Controlled_Buffer controlled_buffer_5
  assign O2 = Enable ? B2 : 1'bz;  // Controlled_Buffer controlled_buffer_6
  assign O1 = Enable ? B1 : 1'bz;  // Controlled_Buffer controlled_buffer_7
  assign O0 = Enable ? B0 : 1'bz;  // Controlled_Buffer controlled_buffer_8
endmodule

module Reverser_8_bits (
  input  I7,
  input  I6,
  input  I5,
  input  I4,
  input  I3,
  input  I2,
  input  I1,
  input  I0,
  output O0,
  output O1,
  output O2,
  output O3,
  output O4,
  output O5,
  output O6,
  output O7
);


  assign O0 = I0;
  assign O1 = I1;
  assign O2 = I2;
  assign O3 = I3;
  assign O4 = I4;
  assign O5 = I5;
  assign O6 = I6;
  assign O7 = I7;
endmodule

module SRAM_16_bytes (
  input  D7,
  input  D6,
  input  D5,
  input  D4,
  input  D3,
  input  D2,
  input  D1,
  input  D0,
  input  write,
  input  read,
  input  clear,
  input  clock,
  input  A3,
  input  A2,
  input  A1,
  input  A0,
  output O7,
  output O6,
  output O5,
  output O4,
  output O3,
  output O2,
  output O1,
  output O0
);

  wire address_decoder_4_bits_1_d0, address_decoder_4_bits_1_d1, address_decoder_4_bits_1_d2,
       address_decoder_4_bits_1_d3, address_decoder_4_bits_1_d4, address_decoder_4_bits_1_d5,
       address_decoder_4_bits_1_d6, address_decoder_4_bits_1_d7, address_decoder_4_bits_1_d8,
       address_decoder_4_bits_1_d9, address_decoder_4_bits_1_da, address_decoder_4_bits_1_db,
       address_decoder_4_bits_1_dc, address_decoder_4_bits_1_dd, address_decoder_4_bits_1_de,
       address_decoder_4_bits_1_df, and_1_out, and_2_out, and_3_out, and_4_out, and_5_out, and_6_out,
       and_7_out, and_8_out, and_9_out, and_10_out, and_11_out, and_12_out, and_13_out, and_14_out,
       and_15_out, and_16_out, and_17_out, and_18_out, and_19_out, and_20_out, and_21_out, and_22_out,
       and_23_out, and_24_out, and_25_out, and_26_out, and_27_out, and_28_out, and_29_out, and_30_out,
       and_31_out, and_32_out, register_8_bits_1_b0, register_8_bits_1_b1, register_8_bits_1_b2,
       register_8_bits_1_b3, register_8_bits_1_b4, register_8_bits_1_b5, register_8_bits_1_b6,
       register_8_bits_1_b7, register_8_bits_1_o0, register_8_bits_1_o1, register_8_bits_1_o2,
       register_8_bits_1_o3, register_8_bits_1_o4, register_8_bits_1_o5, register_8_bits_1_o6,
       register_8_bits_1_o7, register_8_bits_2_b0, register_8_bits_2_b1, register_8_bits_2_b2,
       register_8_bits_2_b3, register_8_bits_2_b4, register_8_bits_2_b5, register_8_bits_2_b6,
       register_8_bits_2_b7, register_8_bits_3_b0, register_8_bits_3_b1, register_8_bits_3_b2,
       register_8_bits_3_b3, register_8_bits_3_b4, register_8_bits_3_b5, register_8_bits_3_b6,
       register_8_bits_3_b7, register_8_bits_4_b0, register_8_bits_4_b1, register_8_bits_4_b2,
       register_8_bits_4_b3, register_8_bits_4_b4, register_8_bits_4_b5, register_8_bits_4_b6,
       register_8_bits_4_b7, register_8_bits_5_b0, register_8_bits_5_b1, register_8_bits_5_b2,
       register_8_bits_5_b3, register_8_bits_5_b4, register_8_bits_5_b5, register_8_bits_5_b6,
       register_8_bits_5_b7, register_8_bits_6_b0, register_8_bits_6_b1, register_8_bits_6_b2,
       register_8_bits_6_b3, register_8_bits_6_b4, register_8_bits_6_b5, register_8_bits_6_b6,
       register_8_bits_6_b7, register_8_bits_7_b0, register_8_bits_7_b1, register_8_bits_7_b2,
       register_8_bits_7_b3, register_8_bits_7_b4, register_8_bits_7_b5, register_8_bits_7_b6,
       register_8_bits_7_b7, register_8_bits_8_b0, register_8_bits_8_b1, register_8_bits_8_b2,
       register_8_bits_8_b3, register_8_bits_8_b4, register_8_bits_8_b5, register_8_bits_8_b6,
       register_8_bits_8_b7, register_8_bits_9_b0, register_8_bits_9_b1, register_8_bits_9_b2,
       register_8_bits_9_b3, register_8_bits_9_b4, register_8_bits_9_b5, register_8_bits_9_b6,
       register_8_bits_9_b7, register_8_bits_10_b0, register_8_bits_10_b1, register_8_bits_10_b2,
       register_8_bits_10_b3, register_8_bits_10_b4, register_8_bits_10_b5, register_8_bits_10_b6,
       register_8_bits_10_b7, register_8_bits_11_b0, register_8_bits_11_b1, register_8_bits_11_b2,
       register_8_bits_11_b3, register_8_bits_11_b4, register_8_bits_11_b5, register_8_bits_11_b6,
       register_8_bits_11_b7, register_8_bits_12_b0, register_8_bits_12_b1, register_8_bits_12_b2,
       register_8_bits_12_b3, register_8_bits_12_b4, register_8_bits_12_b5, register_8_bits_12_b6,
       register_8_bits_12_b7, register_8_bits_13_b0, register_8_bits_13_b1, register_8_bits_13_b2,
       register_8_bits_13_b3, register_8_bits_13_b4, register_8_bits_13_b5, register_8_bits_13_b6,
       register_8_bits_13_b7, register_8_bits_14_b0, register_8_bits_14_b1, register_8_bits_14_b2,
       register_8_bits_14_b3, register_8_bits_14_b4, register_8_bits_14_b5, register_8_bits_14_b6,
       register_8_bits_14_b7, register_8_bits_15_b0, register_8_bits_15_b1, register_8_bits_15_b2,
       register_8_bits_15_b3, register_8_bits_15_b4, register_8_bits_15_b5, register_8_bits_15_b6,
       register_8_bits_15_b7, register_8_bits_16_b0, register_8_bits_16_b1, register_8_bits_16_b2,
       register_8_bits_16_b3, register_8_bits_16_b4, register_8_bits_16_b5, register_8_bits_16_b6,
       register_8_bits_16_b7;

  Address_Decoder_4_bits address_decoder_4_bits_1 (
    .Enable(1'b1), .A1(A1), .A0(A0), .A3(A3), .A2(A2), .DF(address_decoder_4_bits_1_df),
    .DE(address_decoder_4_bits_1_de), .DD(address_decoder_4_bits_1_dd), .DC(address_decoder_4_bits_1_dc),
    .DB(address_decoder_4_bits_1_db), .DA(address_decoder_4_bits_1_da), .D9(address_decoder_4_bits_1_d9),
    .D8(address_decoder_4_bits_1_d8), .D7(address_decoder_4_bits_1_d7), .D6(address_decoder_4_bits_1_d6),
    .D5(address_decoder_4_bits_1_d5), .D4(address_decoder_4_bits_1_d4), .D3(address_decoder_4_bits_1_d3),
    .D2(address_decoder_4_bits_1_d2), .D1(address_decoder_4_bits_1_d1), .D0(address_decoder_4_bits_1_d0));
  Register_8_bits register_8_bits_1 (
    .I7(register_8_bits_1_o7), .I6(register_8_bits_1_o6), .I5(register_8_bits_1_o5),
    .I4(register_8_bits_1_o4), .I3(register_8_bits_1_o3), .I2(register_8_bits_1_o2),
    .I1(register_8_bits_1_o1), .I0(register_8_bits_1_o0), .Clock(clock), .Load(and_4_out), .Reset(clear),
    .Enable(and_1_out), .B7(register_8_bits_1_b7), .B6(register_8_bits_1_b6), .B5(register_8_bits_1_b5),
    .B4(register_8_bits_1_b4), .B3(register_8_bits_1_b3), .B2(register_8_bits_1_b2),
    .B1(register_8_bits_1_b1), .B0(register_8_bits_1_b0), .O7(register_8_bits_1_o7),
    .O6(register_8_bits_1_o6), .O5(register_8_bits_1_o5), .O4(register_8_bits_1_o4),
    .O3(register_8_bits_1_o3), .O2(register_8_bits_1_o2), .O1(register_8_bits_1_o1), .O0(register_8_bits_1_o0));
  and and_1 (and_1_out, read, address_decoder_4_bits_1_d8);
  assign O7 = read ? register_8_bits_1_o7 : 1'bz;  // Controlled_Buffer controlled_buffer_1
  assign O6 = read ? register_8_bits_1_o6 : 1'bz;  // Controlled_Buffer controlled_buffer_2
  assign O5 = read ? register_8_bits_1_o5 : 1'bz;  // Controlled_Buffer controlled_buffer_3
  assign O4 = read ? register_8_bits_1_o4 : 1'bz;  // Controlled_Buffer controlled_buffer_4
  and and_2 (and_2_out, write, address_decoder_4_bits_1_d0);
  and and_3 (and_3_out, read, read);
  DotMatrix #(.dotshape("circle"), .matrixcols(8), .matrixrows(1)) dotmatrix_1 (
    .col0(register_8_bits_2_b7), .col1(register_8_bits_2_b6), .col2(register_8_bits_2_b5),
    .col3(register_8_bits_2_b4), .col4(register_8_bits_2_b3), .col5(register_8_bits_2_b2),
    .col6(register_8_bits_2_b1), .col7(register_8_bits_2_b0));
  DotMatrix #(.dotshape("circle"), .matrixcols(8), .matrixrows(1)) dotmatrix_2 (
    .col0(register_8_bits_1_b0), .col1(register_8_bits_1_b1), .col2(register_8_bits_1_b2),
    .col3(register_8_bits_1_b3), .col4(register_8_bits_1_b4), .col5(register_8_bits_1_b5),
    .col6(register_8_bits_1_b6), .col7(register_8_bits_1_b7));
  assign O3 = read ? register_8_bits_1_o3 : 1'bz;  // Controlled_Buffer controlled_buffer_5
  assign O2 = read ? register_8_bits_1_o2 : 1'bz;  // Controlled_Buffer controlled_buffer_6
  assign O1 = read ? register_8_bits_1_o1 : 1'bz;  // Controlled_Buffer controlled_buffer_7
  assign O0 = read ? register_8_bits_1_o0 : 1'bz;  // Controlled_Buffer controlled_buffer_8
  Register_8_bits register_8_bits_2 (
    .I7(register_8_bits_1_o7), .I6(register_8_bits_1_o6), .I5(register_8_bits_1_o5),
    .I4(register_8_bits_1_o4), .I3(register_8_bits_1_o3), .I2(register_8_bits_1_o2),
    .I1(register_8_bits_1_o1), .I0(register_8_bits_1_o0), .Clock(clock), .Load(and_2_out), .Reset(clear),
    .Enable(and_3_out), .B7(register_8_bits_2_b7), .B6(register_8_bits_2_b6), .B5(register_8_bits_2_b5),
    .B4(register_8_bits_2_b4), .B3(register_8_bits_2_b3), .B2(register_8_bits_2_b2),
    .B1(register_8_bits_2_b1), .B0(register_8_bits_2_b0), .O7(register_8_bits_1_o7),
    .O6(register_8_bits_1_o6), .O5(register_8_bits_1_o5), .O4(register_8_bits_1_o4),
    .O3(register_8_bits_1_o3), .O2(register_8_bits_1_o2), .O1(register_8_bits_1_o1), .O0(register_8_bits_1_o0));
  and and_4 (and_4_out, write, address_decoder_4_bits_1_d8);
  assign register_8_bits_1_o7 = write ? D7 : 1'bz;  // Controlled_Buffer controlled_buffer_9
  assign register_8_bits_1_o6 = write ? D6 : 1'bz;  // Controlled_Buffer controlled_buffer_10
  and and_5 (and_5_out, write, address_decoder_4_bits_1_d1);
  DotMatrix #(.dotshape("circle"), .matrixcols(8), .matrixrows(1)) dotmatrix_3 (
    .col0(register_8_bits_4_b7), .col1(register_8_bits_4_b6), .col2(register_8_bits_4_b5),
    .col3(register_8_bits_4_b4), .col4(register_8_bits_4_b3), .col5(register_8_bits_4_b2),
    .col6(register_8_bits_4_b1), .col7(register_8_bits_4_b0));
  DotMatrix #(.dotshape("circle"), .matrixcols(8), .matrixrows(1)) dotmatrix_4 (
    .col0(register_8_bits_3_b0), .col1(register_8_bits_3_b1), .col2(register_8_bits_3_b2),
    .col3(register_8_bits_3_b3), .col4(register_8_bits_3_b4), .col5(register_8_bits_3_b5),
    .col6(register_8_bits_3_b6), .col7(register_8_bits_3_b7));
  Register_8_bits register_8_bits_3 (
    .I7(register_8_bits_1_o7), .I6(register_8_bits_1_o6), .I5(register_8_bits_1_o5),
    .I4(register_8_bits_1_o4), .I3(register_8_bits_1_o3), .I2(register_8_bits_1_o2),
    .I1(register_8_bits_1_o1), .I0(register_8_bits_1_o0), .Clock(clock), .Load(and_8_out), .Reset(clear),
    .Enable(and_6_out), .B7(register_8_bits_3_b7), .B6(register_8_bits_3_b6), .B5(register_8_bits_3_b5),
    .B4(register_8_bits_3_b4), .B3(register_8_bits_3_b3), .B2(register_8_bits_3_b2),
    .B1(register_8_bits_3_b1), .B0(register_8_bits_3_b0), .O7(register_8_bits_1_o7),
    .O6(register_8_bits_1_o6), .O5(register_8_bits_1_o5), .O4(register_8_bits_1_o4),
    .O3(register_8_bits_1_o3), .O2(register_8_bits_1_o2), .O1(register_8_bits_1_o1), .O0(register_8_bits_1_o0));
  and and_6 (and_6_out, read, address_decoder_4_bits_1_d9);
  assign register_8_bits_1_o5 = write ? D5 : 1'bz;  // Controlled_Buffer controlled_buffer_11
  assign register_8_bits_1_o4 = write ? D4 : 1'bz;  // Controlled_Buffer controlled_buffer_12
  assign register_8_bits_1_o3 = write ? D3 : 1'bz;  // Controlled_Buffer controlled_buffer_13
  assign register_8_bits_1_o2 = write ? D2 : 1'bz;  // Controlled_Buffer controlled_buffer_14
  and and_7 (and_7_out, read, read);
  Register_8_bits register_8_bits_4 (
    .I7(register_8_bits_1_o7), .I6(register_8_bits_1_o6), .I5(register_8_bits_1_o5),
    .I4(register_8_bits_1_o4), .I3(register_8_bits_1_o3), .I2(register_8_bits_1_o2),
    .I1(register_8_bits_1_o1), .I0(register_8_bits_1_o0), .Clock(clock), .Load(and_5_out), .Reset(clear),
    .Enable(and_7_out), .B7(register_8_bits_4_b7), .B6(register_8_bits_4_b6), .B5(register_8_bits_4_b5),
    .B4(register_8_bits_4_b4), .B3(register_8_bits_4_b3), .B2(register_8_bits_4_b2),
    .B1(register_8_bits_4_b1), .B0(register_8_bits_4_b0), .O7(register_8_bits_1_o7),
    .O6(register_8_bits_1_o6), .O5(register_8_bits_1_o5), .O4(register_8_bits_1_o4),
    .O3(register_8_bits_1_o3), .O2(register_8_bits_1_o2), .O1(register_8_bits_1_o1), .O0(register_8_bits_1_o0));
  and and_8 (and_8_out, write, address_decoder_4_bits_1_d9);
  assign register_8_bits_1_o1 = write ? D1 : 1'bz;  // Controlled_Buffer controlled_buffer_15
  assign register_8_bits_1_o0 = write ? D0 : 1'bz;  // Controlled_Buffer controlled_buffer_16
  and and_9 (and_9_out, write, address_decoder_4_bits_1_d2);
  DotMatrix #(.dotshape("circle"), .matrixcols(8), .matrixrows(1)) dotmatrix_5 (
    .col0(register_8_bits_6_b7), .col1(register_8_bits_6_b6), .col2(register_8_bits_6_b5),
    .col3(register_8_bits_6_b4), .col4(register_8_bits_6_b3), .col5(register_8_bits_6_b2),
    .col6(register_8_bits_6_b1), .col7(register_8_bits_6_b0));
  DotMatrix #(.dotshape("circle"), .matrixcols(8), .matrixrows(1)) dotmatrix_6 (
    .col0(register_8_bits_5_b0), .col1(register_8_bits_5_b1), .col2(register_8_bits_5_b2),
    .col3(register_8_bits_5_b3), .col4(register_8_bits_5_b4), .col5(register_8_bits_5_b5),
    .col6(register_8_bits_5_b6), .col7(register_8_bits_5_b7));
  Register_8_bits register_8_bits_5 (
    .I7(register_8_bits_1_o7), .I6(register_8_bits_1_o6), .I5(register_8_bits_1_o5),
    .I4(register_8_bits_1_o4), .I3(register_8_bits_1_o3), .I2(register_8_bits_1_o2),
    .I1(register_8_bits_1_o1), .I0(register_8_bits_1_o0), .Clock(clock), .Load(and_12_out), .Reset(clear),
    .Enable(and_10_out), .B7(register_8_bits_5_b7), .B6(register_8_bits_5_b6), .B5(register_8_bits_5_b5),
    .B4(register_8_bits_5_b4), .B3(register_8_bits_5_b3), .B2(register_8_bits_5_b2),
    .B1(register_8_bits_5_b1), .B0(register_8_bits_5_b0), .O7(register_8_bits_1_o7),
    .O6(register_8_bits_1_o6), .O5(register_8_bits_1_o5), .O4(register_8_bits_1_o4),
    .O3(register_8_bits_1_o3), .O2(register_8_bits_1_o2), .O1(register_8_bits_1_o1), .O0(register_8_bits_1_o0));
  and and_10 (and_10_out, read, address_decoder_4_bits_1_da);
  and and_11 (and_11_out, read, read);
  Register_8_bits register_8_bits_6 (
    .I7(register_8_bits_1_o7), .I6(register_8_bits_1_o6), .I5(register_8_bits_1_o5),
    .I4(register_8_bits_1_o4), .I3(register_8_bits_1_o3), .I2(register_8_bits_1_o2),
    .I1(register_8_bits_1_o1), .I0(register_8_bits_1_o0), .Clock(clock), .Load(and_9_out), .Reset(clear),
    .Enable(and_11_out), .B7(register_8_bits_6_b7), .B6(register_8_bits_6_b6), .B5(register_8_bits_6_b5),
    .B4(register_8_bits_6_b4), .B3(register_8_bits_6_b3), .B2(register_8_bits_6_b2),
    .B1(register_8_bits_6_b1), .B0(register_8_bits_6_b0), .O7(register_8_bits_1_o7),
    .O6(register_8_bits_1_o6), .O5(register_8_bits_1_o5), .O4(register_8_bits_1_o4),
    .O3(register_8_bits_1_o3), .O2(register_8_bits_1_o2), .O1(register_8_bits_1_o1), .O0(register_8_bits_1_o0));
  and and_12 (and_12_out, write, address_decoder_4_bits_1_da);
  DotMatrix #(.dotshape("circle"), .matrixcols(8), .matrixrows(1)) dotmatrix_7 (
    .col0(register_8_bits_8_b7), .col1(register_8_bits_8_b6), .col2(register_8_bits_8_b5),
    .col3(register_8_bits_8_b4), .col4(register_8_bits_8_b3), .col5(register_8_bits_8_b2),
    .col6(register_8_bits_8_b1), .col7(register_8_bits_8_b0));
  DotMatrix #(.dotshape("circle"), .matrixcols(8), .matrixrows(1)) dotmatrix_8 (
    .col0(register_8_bits_7_b0), .col1(register_8_bits_7_b1), .col2(register_8_bits_7_b2),
    .col3(register_8_bits_7_b3), .col4(register_8_bits_7_b4), .col5(register_8_bits_7_b5),
    .col6(register_8_bits_7_b6), .col7(register_8_bits_7_b7));
  Register_8_bits register_8_bits_7 (
    .I7(register_8_bits_1_o7), .I6(register_8_bits_1_o6), .I5(register_8_bits_1_o5),
    .I4(register_8_bits_1_o4), .I3(register_8_bits_1_o3), .I2(register_8_bits_1_o2),
    .I1(register_8_bits_1_o1), .I0(register_8_bits_1_o0), .Clock(clock), .Load(and_16_out), .Reset(clear),
    .Enable(and_13_out), .B7(register_8_bits_7_b7), .B6(register_8_bits_7_b6), .B5(register_8_bits_7_b5),
    .B4(register_8_bits_7_b4), .B3(register_8_bits_7_b3), .B2(register_8_bits_7_b2),
    .B1(register_8_bits_7_b1), .B0(register_8_bits_7_b0), .O7(register_8_bits_1_o7),
    .O6(register_8_bits_1_o6), .O5(register_8_bits_1_o5), .O4(register_8_bits_1_o4),
    .O3(register_8_bits_1_o3), .O2(register_8_bits_1_o2), .O1(register_8_bits_1_o1), .O0(register_8_bits_1_o0));
  and and_13 (and_13_out, read, address_decoder_4_bits_1_db);
  and and_14 (and_14_out, write, address_decoder_4_bits_1_d3);
  and and_15 (and_15_out, read, read);
  Register_8_bits register_8_bits_8 (
    .I7(register_8_bits_1_o7), .I6(register_8_bits_1_o6), .I5(register_8_bits_1_o5),
    .I4(register_8_bits_1_o4), .I3(register_8_bits_1_o3), .I2(register_8_bits_1_o2),
    .I1(register_8_bits_1_o1), .I0(register_8_bits_1_o0), .Clock(clock), .Load(and_14_out), .Reset(clear),
    .Enable(and_15_out), .B7(register_8_bits_8_b7), .B6(register_8_bits_8_b6), .B5(register_8_bits_8_b5),
    .B4(register_8_bits_8_b4), .B3(register_8_bits_8_b3), .B2(register_8_bits_8_b2),
    .B1(register_8_bits_8_b1), .B0(register_8_bits_8_b0), .O7(register_8_bits_1_o7),
    .O6(register_8_bits_1_o6), .O5(register_8_bits_1_o5), .O4(register_8_bits_1_o4),
    .O3(register_8_bits_1_o3), .O2(register_8_bits_1_o2), .O1(register_8_bits_1_o1), .O0(register_8_bits_1_o0));
  and and_16 (and_16_out, write, address_decoder_4_bits_1_db);
  and and_17 (and_17_out, write, address_decoder_4_bits_1_d4);
  DotMatrix #(.dotshape("circle"), .matrixcols(8), .matrixrows(1)) dotmatrix_9 (
    .col0(register_8_bits_10_b7), .col1(register_8_bits_10_b6), .col2(register_8_bits_10_b5),
    .col3(register_8_bits_10_b4), .col4(register_8_bits_10_b3), .col5(register_8_bits_10_b2),
    .col6(register_8_bits_10_b1), .col7(register_8_bits_10_b0));
  DotMatrix #(.dotshape("circle"), .matrixcols(8), .matrixrows(1)) dotmatrix_10 (
    .col0(register_8_bits_9_b0), .col1(register_8_bits_9_b1), .col2(register_8_bits_9_b2),
    .col3(register_8_bits_9_b3), .col4(register_8_bits_9_b4), .col5(register_8_bits_9_b5),
    .col6(register_8_bits_9_b6), .col7(register_8_bits_9_b7));
  Register_8_bits register_8_bits_9 (
    .I7(register_8_bits_1_o7), .I6(register_8_bits_1_o6), .I5(register_8_bits_1_o5),
    .I4(register_8_bits_1_o4), .I3(register_8_bits_1_o3), .I2(register_8_bits_1_o2),
    .I1(register_8_bits_1_o1), .I0(register_8_bits_1_o0), .Clock(clock), .Load(and_20_out), .Reset(clear),
    .Enable(and_18_out), .B7(register_8_bits_9_b7), .B6(register_8_bits_9_b6), .B5(register_8_bits_9_b5),
    .B4(register_8_bits_9_b4), .B3(register_8_bits_9_b3), .B2(register_8_bits_9_b2),
    .B1(register_8_bits_9_b1), .B0(register_8_bits_9_b0), .O7(register_8_bits_1_o7),
    .O6(register_8_bits_1_o6), .O5(register_8_bits_1_o5), .O4(register_8_bits_1_o4),
    .O3(register_8_bits_1_o3), .O2(register_8_bits_1_o2), .O1(register_8_bits_1_o1), .O0(register_8_bits_1_o0));
  and and_18 (and_18_out, read, address_decoder_4_bits_1_dc);
  and and_19 (and_19_out, read, read);
  Register_8_bits register_8_bits_10 (
    .I7(register_8_bits_1_o7), .I6(register_8_bits_1_o6), .I5(register_8_bits_1_o5),
    .I4(register_8_bits_1_o4), .I3(register_8_bits_1_o3), .I2(register_8_bits_1_o2),
    .I1(register_8_bits_1_o1), .I0(register_8_bits_1_o0), .Clock(clock), .Load(and_17_out), .Reset(clear),
    .Enable(and_19_out), .B7(register_8_bits_10_b7), .B6(register_8_bits_10_b6), .B5(register_8_bits_10_b5),
    .B4(register_8_bits_10_b4), .B3(register_8_bits_10_b3), .B2(register_8_bits_10_b2),
    .B1(register_8_bits_10_b1), .B0(register_8_bits_10_b0), .O7(register_8_bits_1_o7),
    .O6(register_8_bits_1_o6), .O5(register_8_bits_1_o5), .O4(register_8_bits_1_o4),
    .O3(register_8_bits_1_o3), .O2(register_8_bits_1_o2), .O1(register_8_bits_1_o1), .O0(register_8_bits_1_o0));
  and and_20 (and_20_out, write, address_decoder_4_bits_1_dc);
  and and_21 (and_21_out, write, address_decoder_4_bits_1_d5);
  DotMatrix #(.dotshape("circle"), .matrixcols(8), .matrixrows(1)) dotmatrix_11 (
    .col0(register_8_bits_12_b7), .col1(register_8_bits_12_b6), .col2(register_8_bits_12_b5),
    .col3(register_8_bits_12_b4), .col4(register_8_bits_12_b3), .col5(register_8_bits_12_b2),
    .col6(register_8_bits_12_b1), .col7(register_8_bits_12_b0));
  DotMatrix #(.dotshape("circle"), .matrixcols(8), .matrixrows(1)) dotmatrix_12 (
    .col0(register_8_bits_11_b0), .col1(register_8_bits_11_b1), .col2(register_8_bits_11_b2),
    .col3(register_8_bits_11_b3), .col4(register_8_bits_11_b4), .col5(register_8_bits_11_b5),
    .col6(register_8_bits_11_b6), .col7(register_8_bits_11_b7));
  Register_8_bits register_8_bits_11 (
    .I7(register_8_bits_1_o7), .I6(register_8_bits_1_o6), .I5(register_8_bits_1_o5),
    .I4(register_8_bits_1_o4), .I3(register_8_bits_1_o3), .I2(register_8_bits_1_o2),
    .I1(register_8_bits_1_o1), .I0(register_8_bits_1_o0), .Clock(clock), .Load(and_24_out), .Reset(clear),
    .Enable(and_22_out), .B7(register_8_bits_11_b7), .B6(register_8_bits_11_b6), .B5(register_8_bits_11_b5),
    .B4(register_8_bits_11_b4), .B3(register_8_bits_11_b3), .B2(register_8_bits_11_b2),
    .B1(register_8_bits_11_b1), .B0(register_8_bits_11_b0), .O7(register_8_bits_1_o7),
    .O6(register_8_bits_1_o6), .O5(register_8_bits_1_o5), .O4(register_8_bits_1_o4),
    .O3(register_8_bits_1_o3), .O2(register_8_bits_1_o2), .O1(register_8_bits_1_o1), .O0(register_8_bits_1_o0));
  and and_22 (and_22_out, read, address_decoder_4_bits_1_dd);
  and and_23 (and_23_out, read, read);
  Register_8_bits register_8_bits_12 (
    .I7(register_8_bits_1_o7), .I6(register_8_bits_1_o6), .I5(register_8_bits_1_o5),
    .I4(register_8_bits_1_o4), .I3(register_8_bits_1_o3), .I2(register_8_bits_1_o2),
    .I1(register_8_bits_1_o1), .I0(register_8_bits_1_o0), .Clock(clock), .Load(and_21_out), .Reset(clear),
    .Enable(and_23_out), .B7(register_8_bits_12_b7), .B6(register_8_bits_12_b6), .B5(register_8_bits_12_b5),
    .B4(register_8_bits_12_b4), .B3(register_8_bits_12_b3), .B2(register_8_bits_12_b2),
    .B1(register_8_bits_12_b1), .B0(register_8_bits_12_b0), .O7(register_8_bits_1_o7),
    .O6(register_8_bits_1_o6), .O5(register_8_bits_1_o5), .O4(register_8_bits_1_o4),
    .O3(register_8_bits_1_o3), .O2(register_8_bits_1_o2), .O1(register_8_bits_1_o1), .O0(register_8_bits_1_o0));
  and and_24 (and_24_out, write, address_decoder_4_bits_1_dd);
  and and_25 (and_25_out, write, address_decoder_4_bits_1_d6);
  DotMatrix #(.dotshape("circle"), .matrixcols(8), .matrixrows(1)) dotmatrix_13 (
    .col0(register_8_bits_14_b7), .col1(register_8_bits_14_b6), .col2(register_8_bits_14_b5),
    .col3(register_8_bits_14_b4), .col4(register_8_bits_14_b3), .col5(register_8_bits_14_b2),
    .col6(register_8_bits_14_b1), .col7(register_8_bits_14_b0));
  DotMatrix #(.dotshape("circle"), .matrixcols(8), .matrixrows(1)) dotmatrix_14 (
    .col0(register_8_bits_13_b0), .col1(register_8_bits_13_b1), .col2(register_8_bits_13_b2),
    .col3(register_8_bits_13_b3), .col4(register_8_bits_13_b4), .col5(register_8_bits_13_b5),
    .col6(register_8_bits_13_b6), .col7(register_8_bits_13_b7));
  Register_8_bits register_8_bits_13 (
    .I7(register_8_bits_1_o7), .I6(register_8_bits_1_o6), .I5(register_8_bits_1_o5),
    .I4(register_8_bits_1_o4), .I3(register_8_bits_1_o3), .I2(register_8_bits_1_o2),
    .I1(register_8_bits_1_o1), .I0(register_8_bits_1_o0), .Clock(clock), .Load(and_28_out), .Reset(clear),
    .Enable(and_26_out), .B7(register_8_bits_13_b7), .B6(register_8_bits_13_b6), .B5(register_8_bits_13_b5),
    .B4(register_8_bits_13_b4), .B3(register_8_bits_13_b3), .B2(register_8_bits_13_b2),
    .B1(register_8_bits_13_b1), .B0(register_8_bits_13_b0), .O7(register_8_bits_1_o7),
    .O6(register_8_bits_1_o6), .O5(register_8_bits_1_o5), .O4(register_8_bits_1_o4),
    .O3(register_8_bits_1_o3), .O2(register_8_bits_1_o2), .O1(register_8_bits_1_o1), .O0(register_8_bits_1_o0));
  and and_26 (and_26_out, read, address_decoder_4_bits_1_de);
  and and_27 (and_27_out, read, read);
  Register_8_bits register_8_bits_14 (
    .I7(register_8_bits_1_o7), .I6(register_8_bits_1_o6), .I5(register_8_bits_1_o5),
    .I4(register_8_bits_1_o4), .I3(register_8_bits_1_o3), .I2(register_8_bits_1_o2),
    .I1(register_8_bits_1_o1), .I0(register_8_bits_1_o0), .Clock(clock), .Load(and_25_out), .Reset(clear),
    .Enable(and_27_out), .B7(register_8_bits_14_b7), .B6(register_8_bits_14_b6), .B5(register_8_bits_14_b5),
    .B4(register_8_bits_14_b4), .B3(register_8_bits_14_b3), .B2(register_8_bits_14_b2),
    .B1(register_8_bits_14_b1), .B0(register_8_bits_14_b0), .O7(register_8_bits_1_o7),
    .O6(register_8_bits_1_o6), .O5(register_8_bits_1_o5), .O4(register_8_bits_1_o4),
    .O3(register_8_bits_1_o3), .O2(register_8_bits_1_o2), .O1(register_8_bits_1_o1), .O0(register_8_bits_1_o0));
  and and_28 (and_28_out, write, address_decoder_4_bits_1_de);
  and and_29 (and_29_out, write, address_decoder_4_bits_1_d7);
  DotMatrix #(.dotshape("circle"), .matrixcols(8), .matrixrows(1)) dotmatrix_15 (
    .col0(register_8_bits_16_b7), .col1(register_8_bits_16_b6), .col2(register_8_bits_16_b5),
    .col3(register_8_bits_16_b4), .col4(register_8_bits_16_b3), .col5(register_8_bits_16_b2),
    .col6(register_8_bits_16_b1), .col7(register_8_bits_16_b0));
  DotMatrix #(.dotshape("circle"), .matrixcols(8), .matrixrows(1)) dotmatrix_16 (
    .col0(register_8_bits_15_b0), .col1(register_8_bits_15_b1), .col2(register_8_bits_15_b2),
    .col3(register_8_bits_15_b3), .col4(register_8_bits_15_b4), .col5(register_8_bits_15_b5),
    .col6(register_8_bits_15_b6), .col7(register_8_bits_15_b7));
  Register_8_bits register_8_bits_15 (
    .I7(register_8_bits_1_o7), .I6(register_8_bits_1_o6), .I5(register_8_bits_1_o5),
    .I4(register_8_bits_1_o4), .I3(register_8_bits_1_o3), .I2(register_8_bits_1_o2),
    .I1(register_8_bits_1_o1), .I0(register_8_bits_1_o0), .Clock(clock), .Load(and_32_out), .Reset(clear),
    .Enable(and_30_out), .B7(register_8_bits_15_b7), .B6(register_8_bits_15_b6), .B5(register_8_bits_15_b5),
    .B4(register_8_bits_15_b4), .B3(register_8_bits_15_b3), .B2(register_8_bits_15_b2),
    .B1(register_8_bits_15_b1), .B0(register_8_bits_15_b0), .O7(register_8_bits_1_o7),
    .O6(register_8_bits_1_o6), .O5(register_8_bits_1_o5), .O4(register_8_bits_1_o4),
    .O3(register_8_bits_1_o3), .O2(register_8_bits_1_o2), .O1(register_8_bits_1_o1), .O0(register_8_bits_1_o0));
  and and_30 (and_30_out, read, address_decoder_4_bits_1_df);
  and and_31 (and_31_out, read, read);
  Register_8_bits register_8_bits_16 (
    .I7(register_8_bits_1_o7), .I6(register_8_bits_1_o6), .I5(register_8_bits_1_o5),
    .I4(register_8_bits_1_o4), .I3(register_8_bits_1_o3), .I2(register_8_bits_1_o2),
    .I1(register_8_bits_1_o1), .I0(register_8_bits_1_o0), .Clock(clock), .Load(and_29_out), .Reset(clear),
    .Enable(and_31_out), .B7(register_8_bits_16_b7), .B6(register_8_bits_16_b6), .B5(register_8_bits_16_b5),
    .B4(register_8_bits_16_b4), .B3(register_8_bits_16_b3), .B2(register_8_bits_16_b2),
    .B1(register_8_bits_16_b1), .B0(register_8_bits_16_b0), .O7(register_8_bits_1_o7),
    .O6(register_8_bits_1_o6), .O5(register_8_bits_1_o5), .O4(register_8_bits_1_o4),
    .O3(register_8_bits_1_o3), .O2(register_8_bits_1_o2), .O1(register_8_bits_1_o1), .O0(register_8_bits_1_o0));
  and and_32 (and_32_out, write, address_decoder_4_bits_1_df);
endmodule

module SRAM_256_bytes (
  input  Write,
  input  Read,
  input  Clock,
  input  Clear,
  input  D7,
  input  D6,
  input  D5,
  input  D4,
  input  D3,
  input  D2,
  input  D1,
  input  D0,
  input  A7,
  input  A6,
  input  A5,
  input  A4,
  input  A3,
  input  A2,
  input  A1,
  input  A0,
  output O7,
  output O6,
  output O5,
  output O4,
  output O3,
  output O2,
  output O1,
  output O0,
  output out_29,
  output out_30,
  output out_31,
  output out_32,
  output out_33,
  output out_34,
  output out_35,
  output out_36
);

  wire address_decoder_4_bits_1_d0, address_decoder_4_bits_1_d1, address_decoder_4_bits_1_d2,
       address_decoder_4_bits_1_d3, address_decoder_4_bits_1_d4, address_decoder_4_bits_1_d5,
       address_decoder_4_bits_1_d6, address_decoder_4_bits_1_d7, address_decoder_4_bits_1_d8,
       address_decoder_4_bits_1_d9, address_decoder_4_bits_1_da, address_decoder_4_bits_1_db,
       address_decoder_4_bits_1_dc, address_decoder_4_bits_1_dd, address_decoder_4_bits_1_de,
       address_decoder_4_bits_1_df, and_1_out, and_2_out, and_3_out, and_4_out, and_5_out, and_6_out,
       and_7_out, and_8_out, and_9_out, and_10_out, and_11_out, and_12_out, and_13_out, and_14_out,
       and_15_out, and_16_out, and_17_out, and_18_out, and_19_out, and_20_out, and_21_out, and_22_out,
       and_23_out, and_24_out, and_25_out, and_26_out, and_27_out, and_28_out, and_29_out, and_30_out,
       and_31_out, and_32_out;

  Address_Decoder_4_bits address_decoder_4_bits_1 (
    .Enable(1'b1), .A1(A5), .A0(A4), .A3(A7), .A2(A6), .DF(address_decoder_4_bits_1_df),
    .DE(address_decoder_4_bits_1_de), .DD(address_decoder_4_bits_1_dd), .DC(address_decoder_4_bits_1_dc),
    .DB(address_decoder_4_bits_1_db), .DA(address_decoder_4_bits_1_da), .D9(address_decoder_4_bits_1_d9),
    .D8(address_decoder_4_bits_1_d8), .D7(address_decoder_4_bits_1_d7), .D6(address_decoder_4_bits_1_d6),
    .D5(address_decoder_4_bits_1_d5), .D4(address_decoder_4_bits_1_d4), .D3(address_decoder_4_bits_1_d3),
    .D2(address_decoder_4_bits_1_d2), .D1(address_decoder_4_bits_1_d1), .D0(address_decoder_4_bits_1_d0));
  and and_1 (and_1_out, Read, address_decoder_4_bits_1_d0);
  and and_2 (and_2_out, Write, address_decoder_4_bits_1_d0);
  and and_3 (and_3_out, Read, address_decoder_4_bits_1_d1);
  and and_4 (and_4_out, Write, address_decoder_4_bits_1_d1);
  and and_5 (and_5_out, Read, address_decoder_4_bits_1_d2);
  and and_6 (and_6_out, Write, address_decoder_4_bits_1_d2);
  and and_7 (and_7_out, Read, address_decoder_4_bits_1_d3);
  and and_8 (and_8_out, Write, address_decoder_4_bits_1_d3);
  and and_9 (and_9_out, Read, address_decoder_4_bits_1_d4);
  and and_10 (and_10_out, Write, address_decoder_4_bits_1_d4);
  and and_11 (and_11_out, Read, address_decoder_4_bits_1_d5);
  and and_12 (and_12_out, Write, address_decoder_4_bits_1_d5);
  and and_13 (and_13_out, Read, address_decoder_4_bits_1_d6);
  and and_14 (and_14_out, Write, address_decoder_4_bits_1_d6);
  and and_15 (and_15_out, Read, address_decoder_4_bits_1_d7);
  and and_16 (and_16_out, Write, address_decoder_4_bits_1_d7);
  SRAM_16_bytes sram_16_bytes_1 (
    .A2(A2), .A1(A1), .A0(A0), .clear(Clear), .clock(Clock), .write(and_2_out), .read(and_1_out),
    .D7(out_29), .D6(out_30), .D5(out_31), .D4(out_32), .D3(out_33), .D2(out_34), .D1(out_35), .D0(out_36),
    .O7(out_29), .O6(out_30), .O5(out_31), .O4(out_32), .O3(out_33), .O2(out_34), .O1(out_35), .O0(out_36));  // open: A3
  SRAM_16_bytes sram_16_bytes_2 (
    .A2(A2), .A1(A1), .A0(A0), .clear(Clear), .clock(Clock), .write(and_4_out), .read(and_3_out),
    .D7(out_29), .D6(out_30), .D5(out_31), .D4(out_32), .D3(out_33), .D2(out_34), .D1(out_35), .D0(out_36),
    .O7(out_29), .O6(out_30), .O5(out_31), .O4(out_32), .O3(out_33), .O2(out_34), .O1(out_35), .O0(out_36));  // open: A3
  SRAM_16_bytes sram_16_bytes_3 (
    .A2(A2), .A1(A1), .A0(A0), .clear(Clear), .clock(Clock), .write(and_6_out), .read(and_5_out),
    .D7(out_29), .D6(out_30), .D5(out_31), .D4(out_32), .D3(out_33), .D2(out_34), .D1(out_35), .D0(out_36),
    .O7(out_29), .O6(out_30), .O5(out_31), .O4(out_32), .O3(out_33), .O2(out_34), .O1(out_35), .O0(out_36));  // open: A3
  SRAM_16_bytes sram_16_bytes_4 (
    .A2(A2), .A1(A1), .A0(A0), .clear(Clear), .clock(Clock), .write(and_8_out), .read(and_7_out),
    .D7(out_29), .D6(out_30), .D5(out_31), .D4(out_32), .D3(out_33), .D2(out_34), .D1(out_35), .D0(out_36),
    .O7(out_29), .O6(out_30), .O5(out_31), .O4(out_32), .O3(out_33), .O2(out_34), .O1(out_35), .O0(out_36));  // open: A3
  SRAM_16_bytes sram_16_bytes_5 (
    .A2(A2), .A1(A1), .A0(A0), .clear(Clear), .clock(Clock), .write(and_10_out), .read(and_9_out),
    .D7(out_29), .D6(out_30), .D5(out_31), .D4(out_32), .D3(out_33), .D2(out_34), .D1(out_35), .D0(out_36),
    .O7(out_29), .O6(out_30), .O5(out_31), .O4(out_32), .O3(out_33), .O2(out_34), .O1(out_35), .O0(out_36));  // open: A3
  SRAM_16_bytes sram_16_bytes_6 (
    .A2(A2), .A1(A1), .A0(A0), .clear(Clear), .clock(Clock), .write(and_12_out), .read(and_11_out),
    .D7(out_29), .D6(out_30), .D5(out_31), .D4(out_32), .D3(out_33), .D2(out_34), .D1(out_35), .D0(out_36),
    .O7(out_29), .O6(out_30), .O5(out_31), .O4(out_32), .O3(out_33), .O2(out_34), .O1(out_35), .O0(out_36));  // open: A3
  SRAM_16_bytes sram_16_bytes_7 (
    .A2(A2), .A1(A1), .A0(A0), .clear(Clear), .clock(Clock), .write(and_14_out), .read(and_13_out),
    .D7(out_29), .D6(out_30), .D5(out_31), .D4(out_32), .D3(out_33), .D2(out_34), .D1(out_35), .D0(out_36),
    .O7(out_29), .O6(out_30), .O5(out_31), .O4(out_32), .O3(out_33), .O2(out_34), .O1(out_35), .O0(out_36));  // open: A3
  SRAM_16_bytes sram_16_bytes_8 (
    .A2(A2), .A1(A1), .A0(A0), .clear(Clear), .clock(Clock), .write(and_16_out), .read(and_15_out),
    .D7(out_29), .D6(out_30), .D5(out_31), .D4(out_32), .D3(out_33), .D2(out_34), .D1(out_35), .D0(out_36),
    .O7(out_36), .O6(out_35), .O5(out_34), .O4(out_33), .O3(out_32), .O2(out_31), .O1(out_30), .O0(out_29));  // open: A3
  assign O7 = Read ? out_29 : 1'bz;  // Controlled_Buffer controlled_buffer_1
  assign O6 = Read ? out_30 : 1'bz;  // Controlled_Buffer controlled_buffer_2
  assign O5 = Read ? out_31 : 1'bz;  // Controlled_Buffer controlled_buffer_3
  assign O4 = Read ? out_32 : 1'bz;  // Controlled_Buffer controlled_buffer_4
  assign O3 = Read ? out_33 : 1'bz;  // Controlled_Buffer controlled_buffer_5
  assign O2 = Read ? out_34 : 1'bz;  // Controlled_Buffer controlled_buffer_6
  assign O1 = Read ? out_35 : 1'bz;  // Controlled_Buffer controlled_buffer_7
  assign O0 = Read ? out_36 : 1'bz;  // Controlled_Buffer controlled_buffer_8
  assign out_29 = Write ? D7 : 1'bz;  // Controlled_Buffer controlled_buffer_9
  assign out_30 = Write ? D6 : 1'bz;  // Controlled_Buffer controlled_buffer_10
  assign out_31 = Write ? D5 : 1'bz;  // Controlled_Buffer controlled_buffer_11
  SRAM_16_bytes sram_16_bytes_9 (
    .A3(A3), .A2(A2), .A1(A1), .A0(A0), .clear(Clear), .clock(Clock), .write(and_17_out), .read(and_18_out),
    .D7(out_29), .D6(out_30), .D5(out_31), .D4(out_32), .D3(out_33), .D2(out_34), .D1(out_35), .D0(out_36),
    .O7(out_29), .O6(out_30), .O5(out_31), .O4(out_32), .O3(out_33), .O2(out_34), .O1(out_35), .O0(out_36));
  SRAM_16_bytes sram_16_bytes_10 (
    .A3(A3), .A2(A2), .A1(A1), .A0(A0), .clear(Clear), .clock(Clock), .write(and_19_out), .read(and_20_out),
    .D7(out_29), .D6(out_30), .D5(out_31), .D4(out_32), .D3(out_33), .D2(out_34), .D1(out_35), .D0(out_36),
    .O7(out_29), .O6(out_30), .O5(out_31), .O4(out_32), .O3(out_33), .O2(out_34), .O1(out_35), .O0(out_36));
  SRAM_16_bytes sram_16_bytes_11 (
    .A3(A3), .A2(A2), .A1(A1), .A0(A0), .clear(Clear), .clock(Clock), .write(and_21_out), .read(and_22_out),
    .D7(out_29), .D6(out_30), .D5(out_31), .D4(out_32), .D3(out_33), .D2(out_34), .D1(out_35), .D0(out_36),
    .O7(out_29), .O6(out_30), .O5(out_31), .O4(out_32), .O3(out_33), .O2(out_34), .O1(out_35), .O0(out_36));
  SRAM_16_bytes sram_16_bytes_12 (
    .A3(A3), .A2(A2), .A1(A1), .A0(A0), .clear(Clear), .clock(Clock), .write(and_23_out), .read(and_24_out),
    .D7(out_29), .D6(out_30), .D5(out_31), .D4(out_32), .D3(out_33), .D2(out_34), .D1(out_35), .D0(out_36),
    .O7(out_29), .O6(out_30), .O5(out_31), .O4(out_32), .O3(out_33), .O2(out_34), .O1(out_35), .O0(out_36));
  SRAM_16_bytes sram_16_bytes_13 (
    .A3(A3), .A2(A2), .A1(A1), .A0(A0), .clear(Clear), .clock(Clock), .write(and_25_out), .read(and_26_out),
    .D7(out_29), .D6(out_30), .D5(out_31), .D4(out_32), .D3(out_33), .D2(out_34), .D1(out_35), .D0(out_36),
    .O7(out_29), .O6(out_30), .O5(out_31), .O4(out_32), .O3(out_33), .O2(out_34), .O1(out_35), .O0(out_36));
  SRAM_16_bytes sram_16_bytes_14 (
    .A3(A3), .A2(A2), .A1(A1), .A0(A0), .clear(Clear), .clock(Clock), .write(and_27_out), .read(and_28_out),
    .D7(out_29), .D6(out_30), .D5(out_31), .D4(out_32), .D3(out_33), .D2(out_34), .D1(out_35), .D0(out_36),
    .O7(out_29), .O6(out_30), .O5(out_31), .O4(out_32), .O3(out_33), .O2(out_34), .O1(out_35), .O0(out_36));
  SRAM_16_bytes sram_16_bytes_15 (
    .A3(A3), .A2(A2), .A1(A1), .A0(A0), .clear(Clear), .clock(Clock), .write(and_29_out), .read(and_30_out),
    .D7(out_29), .D6(out_30), .D5(out_31), .D4(out_32), .D3(out_33), .D2(out_34), .D1(out_35), .D0(out_36),
    .O7(out_29), .O6(out_30), .O5(out_31), .O4(out_32), .O3(out_33), .O2(out_34), .O1(out_35), .O0(out_36));
  SRAM_16_bytes sram_16_bytes_16 (
    .A3(A3), .A2(A2), .A1(A1), .A0(A0), .clear(Clear), .clock(Clock), .write(and_31_out), .read(and_32_out),
    .D7(out_36), .D6(out_35), .D5(out_34), .D4(out_33), .D3(out_32), .D2(out_31), .D1(out_30), .D0(out_29),
    .O7(out_29), .O6(out_30), .O5(out_31), .O4(out_32), .O3(out_33), .O2(out_34), .O1(out_35), .O0(out_36));
  assign out_32 = Write ? D4 : 1'bz;  // Controlled_Buffer controlled_buffer_12
  assign out_33 = Write ? D3 : 1'bz;  // Controlled_Buffer controlled_buffer_13
  assign out_34 = Write ? D2 : 1'bz;  // Controlled_Buffer controlled_buffer_14
  assign out_35 = Write ? D1 : 1'bz;  // Controlled_Buffer controlled_buffer_15
  assign out_36 = Write ? D0 : 1'bz;  // Controlled_Buffer controlled_buffer_16
  and and_17 (and_17_out, Write, address_decoder_4_bits_1_df);
  and and_18 (and_18_out, Read, address_decoder_4_bits_1_df);
  and and_19 (and_19_out, Write, address_decoder_4_bits_1_de);
  and and_20 (and_20_out, Read, address_decoder_4_bits_1_de);
  and and_21 (and_21_out, Write, address_decoder_4_bits_1_dd);
  and and_22 (and_22_out, Read, address_decoder_4_bits_1_dd);
  and and_23 (and_23_out, Write, address_decoder_4_bits_1_dc);
  and and_24 (and_24_out, Read, address_decoder_4_bits_1_dc);
  and and_25 (and_25_out, Write, address_decoder_4_bits_1_db);
  and and_26 (and_26_out, Read, address_decoder_4_bits_1_db);
  and and_27 (and_27_out, Write, address_decoder_4_bits_1_da);
  and and_28 (and_28_out, Read, address_decoder_4_bits_1_da);
  and and_29 (and_29_out, Write, address_decoder_4_bits_1_d9);
  and and_30 (and_30_out, Read, address_decoder_4_bits_1_d9);
  and and_31 (and_31_out, Write, address_decoder_4_bits_1_d8);
  and and_32 (and_32_out, Read, address_decoder_4_bits_1_d8);
endmodule

module Instruction_decoder (
  input  PM,
  input  ZF,
  input  CF,
  input  OP0,
  input  OP1,
  input  OP2,
  input  OP3,
  input  OP4,
  input  Clear,
  input  CLK,
  output OI,
  output JP,
  output CO,
  output CE,
  output IR,
  output II,
  output RR,
  output RW,
  output S7,
  output S6,
  output S5,
  output S4,
  output S3,
  output S2,
  output S1,
  output S0,
  output MI,
  output BO,
  output BI,
  output SU,
  output EO,
  output AO,
  output AI,
  output HL,
  output FI
);

  wire address_decoder_4_bits_1_d8, counter_8_bits_1_o3, not_1_out, not_2_out, not_3_out, or_1_out;
  wire [2:0] counter_8_bits_1_o0;
  wire [16:0] rom_1_data;

  not not_1 (not_1_out, 1'b1);
  not not_2 (not_2_out, CLK);
  or or_1 (or_1_out, Clear, rom_1_data[4], address_decoder_4_bits_1_d8);
  Counter_8_bits counter_8_bits_1 (
    .CEnable(1'b1), .CWrite(not_1_out), .CReset(or_1_out), .Clock(not_2_out), .O3(counter_8_bits_1_o3),
    .O2(counter_8_bits_1_o0[2]), .O1(counter_8_bits_1_o0[1]), .O0(counter_8_bits_1_o0[0]));  // open: I7, I6, I5, I4, I3, I2, I1, I0, O7, O6, O5, O4
  Address_Decoder_4_bits address_decoder_4_bits_1 (
    .Enable(1'b1), .A1(counter_8_bits_1_o0[1]), .A0(counter_8_bits_1_o0[0]), .A3(counter_8_bits_1_o3),
    .A2(counter_8_bits_1_o0[2]), .D8(address_decoder_4_bits_1_d8), .D7(S7), .D6(S6), .D5(S5), .D4(S4),
    .D3(S3), .D2(S2), .D1(S1), .D0(S0));  // open: DF, DE, DD, DC, DB, DA, D9
  ROM #(.addrWidth(10), .dataWidth(17)) rom_1 (
    .addr({OP4, OP3, OP2, OP1, OP0, CF, ZF, counter_8_bits_1_o0}), .data(rom_1_data));
  not not_3 (not_3_out, PM);
  and and_1 (OI, not_3_out, rom_1_data[0]);
  and and_2 (JP, not_3_out, rom_1_data[1]);
  and and_3 (CO, not_3_out, rom_1_data[2]);
  and and_4 (CE, not_3_out, rom_1_data[3]);
  and and_5 (IR, not_3_out, rom_1_data[4]);
  and and_6 (II, not_3_out, rom_1_data[5]);
  and and_7 (RR, not_3_out, rom_1_data[6]);
  and and_8 (RW, not_3_out, rom_1_data[7]);
  and and_9 (MI, not_3_out, rom_1_data[8]);
  and and_10 (BO, not_3_out, rom_1_data[9]);
  and and_11 (BI, not_3_out, rom_1_data[10]);
  and and_12 (SU, not_3_out, rom_1_data[11]);
  and and_13 (EO, not_3_out, rom_1_data[12]);
  and and_14 (AO, not_3_out, rom_1_data[13]);
  and and_15 (AI, not_3_out, rom_1_data[14]);
  and and_16 (HL, not_3_out, rom_1_data[15]);
  and and_17 (FI, not_3_out, rom_1_data[16]);

  // Notes on the sheet:
  //   contents of rom_1 (hex, n*v repeats v):
  //   104 68 10 5*0 104 68 10 5*0 104 68 10 5*0 104 68 10 5*0 104 68 8000 10 4*0 104 68 8000 10 4*0 104 68
  //   8000 10 4*0 104 68 8000 10 4*0 104 68 10c 4040 10 0 0 0 104 68 10c 4040 10 0 0 0 104 68 10c 4040 10
  //   0 0 0 104 68 10c 4040 10 0 0 0 104 68 10c 140 4040 10 0 0 104 68 10c 140 4040 10 0 0 104 68 10c 140
  //   4040 10 0 0 104 68 10c 140 4040 10 0 0 104 68 10c 140 2080 10 0 0 104 68 10c 140 2080 10 0 0 104 68
  //   10c 140 2080 10 0 0 104 68 10c 140 2080 10 0 0 104 68 10c 440 10 0 0 0 104 68 10c 440 10 0 0 0 104
  //   68 10c 440 10 0 0 0 104 68 10c 440 10 0 0 0 104 68 10c 140 440 10 0 0 104 68 10c 140 440 10 0 0 104
  //   68 10c 140 440 10 0 0 104 68 10c 140 440 10 0 0 104 68 10c 140 280 10 0 0 104 68 10c 140 280 10 0 0
  //   104 68 10c 140 280 10 0 0 104 68 10c 140 280 10 0 0 104 68 10c 440 15000 10 0 0 104 68 10c 440 15000
  //   10 0 0 104 68 10c 440 15000 10 0 0 104 68 10c 440 15000 10 0 0 104 68 10c 140 440 15000 10 0 104 68
  //   10c 140 440 15000 10 0 104 68 10c 140 440 15000 10 0 104 68 10c 140 440 15000 10 0 104 68 10c c40
  //   15800 10 0 0 104 68 10c c40 15800 10 0 0 104 68 10c c40 15800 10 0 0 104 68 10c c40 15800 10 0 0 104
  //   68 10c 140 c40 15800 10 0 104 68 10c 140 c40 15800 10 0 104 68 10c 140 c40 15800 10 0 104 68 10c 140
  //   c40 15800 10 0 104 68 2001 10 4*0 104 68 2001 10 4*0 104 68 2001 10 4*0 104 68 2001 10 4*0 104 68
  //   201 10 4*0 104 68 201 10 4*0 104 68 201 10 4*0 104 68 201 10 4*0 104 68 10c 41 10 0 0 0 104 68 10c
  //   41 10 0 0 0 104 68 10c 41 10 0 0 0 104 68 10c 41 10 0 0 0 104 68 10c 140 41 10 0 0 104 68 10c 140 41
  //   10 0 0 104 68 10c 140 41 10 0 0 104 68 10c 140 41 10 0 0 104 68 10c 42 10 0 0 0 104 68 10c 42 10 0 0
  //   0 104 68 10c 42 10 0 0 0 104 68 10c 42 10 0 0 0 104 68 8 10 4*0 104 68 10c 42 10 0 0 0 104 68 8 10
  //   4*0 104 68 10c 42 10 0 0 0 104 68 8 10 4*0 104 68 8 10 4*0 104 68 10c 42 10 0 0 0 104 68 10c 42 10
endmodule

module Decoder_8_bits_to_7_segment (
  input  I0,
  input  I1,
  input  I2,
  input  I3,
  input  I4,
  input  I5,
  input  I6,
  input  I7,
  output a1,
  output b1,
  output c1,
  output d1,
  output e1,
  output f1,
  output g1,
  output a2,
  output b2,
  output c2,
  output d2,
  output e2,
  output f2,
  output g2,
  output a3,
  output b3,
  output c3,
  output d3,
  output e3,
  output f3,
  output g3
);

  ROM #(.dataWidth(21)) rom_1 (
    .addr({I7, I6, I5, I4, I3, I2, I1, I0}),
    .data({g3, f3, e3, d3, c3, b3, a3, g2, f2, e2, d2, c2, b2, a2, g1, f1, e1, d1, c1, b1, a1}));

  // Notes on the sheet:
  //   contents of rom_1 (hex, n*v repeats v):
  //   3f 6 5b 4f 66 6d 7d 7 7f 6f 33f 306 35b 34f 366 36d 37d 307 37f 36f 2dbf 2d86 2ddb 2dcf 2de6 2ded
  //   2dfd 2d87 2dff 2def 27bf 2786 27db 27cf 27e6 27ed 27fd 2787 27ff 27ef 333f 3306 335b 334f 3366 336d
  //   337d 3307 337f 336f 36bf 3686 36db 36cf 36e6 36ed 36fd 3687 36ff 36ef 3ebf 3e86 3edb 3ecf 3ee6 3eed
  //   3efd 3e87 3eff 3eef 3bf 386 3db 3cf 3e6 3ed 3fd 387 3ff 3ef 3fbf 3f86 3fdb 3fcf 3fe6 3fed 3ffd 3f87
  //   3fff 3fef 37bf 3786 37db 37cf 37e6 37ed 37fd 3787 37ff 37ef 19fbf 19f86 19fdb 19fcf 19fe6 19fed
  //   19ffd 19f87 19fff 19fef 1833f 18306 1835b 1834f 18366 1836d 1837d 18307 1837f 1836f 1adbf 1ad86
  //   1addb 1adcf 1ade6 1aded 1adfd 1ad87 1adff 1adef 1a7bf 1a786 1a7db 1a7cf 1a7e6 1a7ed 1a7fd 1a787
  //   1a7ff 1a7ef 1b33f 1b306 1b35b 1b34f 1b366 1b36d 1b37d 1b307 1b37f 1b36f 1b6bf 1b686 1b6db 1b6cf
  //   1b6e6 1b6ed 1b6fd 1b687 1b6ff 1b6ef 1bebf 1be86 1bedb 1becf 1bee6 1beed 1befd 1be87 1beff 1beef
  //   183bf 18386 183db 183cf 183e6 183ed 183fd 18387 183ff 183ef 1bfbf 1bf86 1bfdb 1bfcf 1bfe6 1bfed
  //   1bffd 1bf87 1bfff 1bfef 1b7bf 1b786 1b7db 1b7cf 1b7e6 1b7ed 1b7fd 1b787 1b7ff 1b7ef 16dfbf 16df86
  //   16dfdb 16dfcf 16dfe6 16dfed 16dffd 16df87 16dfff 16dfef 16c33f 16c306 16c35b 16c34f 16c366 16c36d
  //   16c37d 16c307 16c37f 16c36f 16edbf 16ed86 16eddb 16edcf 16ede6 16eded 16edfd 16ed87 16edff 16edef
  //   16e7bf 16e786 16e7db 16e7cf 16e7e6 16e7ed 16e7fd 16e787 16e7ff 16e7ef 16f33f 16f306 16f35b 16f34f
  //   16f366 16f36d 16f37d 16f307 16f37f 16f36f 16f6bf 16f686 16f6db 16f6cf 16f6e6 16f6ed
endmodule

module Program_loader (
  input  Enabled,
  input  [7:0] ROM_data,
  input  Clock,
  input  Reset,
  output [7:0] ROM_addr,
  output O7,
  output O6,
  output O5,
  output O4,
  output O3,
  output O2,
  output O1,
  output O0,
  output Programing,
  output Addr_write,
  output RAM_write
);

  wire j_k_ff_1_q, j_k_ff_1_qn;
  wire [7:0] controlled_buffer_1_out;

  Counter_8_bits counter_8_bits_1 (
    .CEnable(Enabled), .CWrite(1'b0), .CReset(Reset), .Clock(j_k_ff_1_qn), .O7(ROM_addr[7]),
    .O6(ROM_addr[6]), .O5(ROM_addr[5]), .O4(ROM_addr[4]), .O3(ROM_addr[3]), .O2(ROM_addr[2]),
    .O1(ROM_addr[1]), .O0(ROM_addr[0]));  // open: I7, I6, I5, I4, I3, I2, I1, I0
  assign controlled_buffer_1_out = j_k_ff_1_qn ? ROM_addr : 8'bz;  // Controlled_Buffer controlled_buffer_1
  assign controlled_buffer_1_out = j_k_ff_1_q ? ROM_data : 8'bz;  // Controlled_Buffer controlled_buffer_2
  J_K_Flip_Flop j_k_ff_1 (
    .J(Clock), .K(Clock), .clk(Clock), .Q(j_k_ff_1_q), .Qn(j_k_ff_1_qn), .preset(1'b0), .reset(1'b0));
  assign O7 = Enabled ? controlled_buffer_1_out[7] : 1'bz;  // Controlled_Buffer controlled_buffer_3
  assign O6 = Enabled ? controlled_buffer_1_out[6] : 1'bz;  // Controlled_Buffer controlled_buffer_4
  assign O5 = Enabled ? controlled_buffer_1_out[5] : 1'bz;  // Controlled_Buffer controlled_buffer_5
  assign O4 = Enabled ? controlled_buffer_1_out[4] : 1'bz;  // Controlled_Buffer controlled_buffer_6
  assign O3 = Enabled ? controlled_buffer_1_out[3] : 1'bz;  // Controlled_Buffer controlled_buffer_7
  assign O2 = Enabled ? controlled_buffer_1_out[2] : 1'bz;  // Controlled_Buffer controlled_buffer_8
  assign O1 = Enabled ? controlled_buffer_1_out[1] : 1'bz;  // Controlled_Buffer controlled_buffer_9
  assign O0 = Enabled ? controlled_buffer_1_out[0] : 1'bz;  // Controlled_Buffer controlled_buffer_10
  and and_1 (Addr_write, j_k_ff_1_qn, Enabled);
  and and_2 (RAM_write, j_k_ff_1_q, Enabled);

  assign Programing = Enabled;
endmodule

module Register_2_bits (
  input  Clock,
  input  Load,
  input  Reset,
  input  Enable,
  input  I1,
  input  I0,
  output B1,
  output B0,
  output O1,
  output O0
);

  Register #(.width(1)) register_1 (.D(I1), .en(Load), .clk(Clock), .Q(B1), .clr(Reset));
  Register #(.width(1)) register_2 (.D(I0), .en(Load), .clk(Clock), .Q(B0), .clr(Reset));
  assign O1 = Enable ? B1 : 1'bz;  // Controlled_Buffer controlled_buffer_1
  assign O0 = Enable ? B0 : 1'bz;  // Controlled_Buffer controlled_buffer_2
endmodule
